// Logisim project es_primo.circ as structural Verilog: 1 circuit, main circuit main
module main (
  input  [7:0] n,
  input  start,
  input  reset,
  output \output ,
  output \end 
);

  wire a__0, c__n, clock, comparator_1_eq, demultiplexer_1_out0, demultiplexer_2_out0, demultiplexer_3_out1,
       demultiplexer_4_out0, idle_q, if_q, L_a, L_a0, L_a1, L_c, L_c1, or_1_out, or_2_out, or_5_out,
       pre_if_q, restart, while_q;
  wire [7:0] a, c, c__1, multiplexer_1_out, multiplexer_2_out, n_c;

  Divider divider_1 (.a(n), .b(c), .rem(n_c));  // open: out, upper
  D_Flip_Flop idle (.clk(clock), .D(or_1_out), .Q(idle_q), .preset(reset));  // open: Qn, en, reset
  Multiplexer #(.width(8), .enable("false")) multiplexer_1 (
    .in0(8'h2), .in1(c__1), .out(multiplexer_1_out), .sel(L_c1));
  or or_1 (or_1_out, restart, demultiplexer_1_out0);
  Demultiplexer #(.enable("false")) demultiplexer_1 (
    .out0(demultiplexer_1_out0), .out1(L_a0), .in(idle_q), .sel(start));
  Clock clock_1 (.out(clock));
  Register register_1 (.D(multiplexer_1_out), .en(L_c), .Q(c), .clk(clock));  // open: clr
  Comparator #(.mode("unsigned")) comparator_1 (.a(c), .b(n), .eq(comparator_1_eq));  // open: gt, lt
  not not_1 (c__n, comparator_1_eq);
  or or_2 (or_2_out, L_a0, L_c1);
  Adder adder_1 (.a(c), .b(8'h1), .out(c__1));  // open: cin, cout
  Multiplexer #(.width(8), .enable("false")) multiplexer_2 (
    .in0({8{1'b0}}), .in1(n_c), .out(multiplexer_2_out), .sel(L_a1));
  D_Flip_Flop \while  (.clk(clock), .D(or_2_out), .Q(while_q), .reset(reset));  // open: Qn, preset, en
  Demultiplexer #(.enable("false")) demultiplexer_2 (
    .out0(demultiplexer_2_out0), .out1(L_a1), .in(while_q), .sel(c__n));
  Register register_2 (.D(multiplexer_2_out), .en(L_a), .Q(a), .clk(clock));  // open: clr
  Comparator comparator_2 (.a(a), .b({8{1'b0}}), .eq(a__0));  // open: gt, lt
  not not_2 (\output , a__0);
  D_Flip_Flop pre_if (.clk(clock), .D(L_a1), .Q(pre_if_q), .reset(reset));  // open: Qn, preset, en
  or or_3 (L_c, L_a0, L_c1);
  or or_4 (L_a, L_a0, L_a1);
  Demultiplexer #(.enable("false")) demultiplexer_3 (.out0(L_c1), .out1(demultiplexer_3_out1), .in(if_q), .sel(a__0));
  D_Flip_Flop \if  (.clk(clock), .D(pre_if_q), .Q(if_q), .reset(reset));  // open: Qn, preset, en
  D_Flip_Flop u_end (.clk(clock), .D(or_5_out), .Q(\end ), .reset(reset));  // open: Qn, preset, en
  or or_5 (or_5_out, demultiplexer_4_out0, demultiplexer_2_out0, demultiplexer_3_out1);
  Demultiplexer #(.enable("false")) demultiplexer_4 (
    .out0(demultiplexer_4_out0), .out1(restart), .in(\end ), .sel(start));

  // Other names for the same wires on the sheet: L_c0 = L_a0; S_a = L_a1; S_c = L_c1
endmodule
