// Logisim project signed_multiplier.circ as structural Verilog: 4 circuits, main circuit signed_multiplier
module signed_multiplier (
  input  [3:0] multiplicand,
  input  clock,
  input  start,
  input  [3:0] multiplier,
  input  reset,
  output \end ,
  output [7:0] result
);

  wire control_unit_1_l_acc_0, control_unit_1_l_acc_1, control_unit_1_l_acc_2, control_unit_1_l_acc_3,
       control_unit_1_l_counter_0, control_unit_1_l_counter_1, control_unit_1_l_q0, control_unit_1_l_q1,
       control_unit_1_l_q_1, control_unit_1_s_count, control_unit_1_s_q, control_unit_1_s_signal,
       DataPath_count__0, DataPath_l_bit_q, DataPath_q_1;

  control_unit control_unit_1 (
    .clock(clock), .start(start), .reset(reset), .l_bit_Q(DataPath_l_bit_q), .Q_1(DataPath_q_1),
    .count__0(DataPath_count__0), .s_signal(control_unit_1_s_signal), .S_q(control_unit_1_s_q),
    .S_count(control_unit_1_s_count), .\end (\end ), .L_acc_1(control_unit_1_l_acc_1),
    .L_counter_0(control_unit_1_l_counter_0), .L_q0(control_unit_1_l_q0), .L_acc_0(control_unit_1_l_acc_0),
    .L_acc_2(control_unit_1_l_acc_2), .L_acc_3(control_unit_1_l_acc_3), .L_q1(control_unit_1_l_q1),
    .L_counter_1(control_unit_1_l_counter_1), .L_q_1(control_unit_1_l_q_1));
  data_path DataPath (
    .result(result), .Q_1(DataPath_q_1), .s_signal(control_unit_1_s_signal), .l_bit_Q(DataPath_l_bit_q),
    .clock(clock), .reset(reset), .multiplicand(multiplicand), .multiplier(multiplier),
    .count__0(DataPath_count__0), .S_q(control_unit_1_s_q), .S_count(control_unit_1_s_count),
    .L_q_1(control_unit_1_l_q_1), .L_counter_0(control_unit_1_l_counter_0),
    .L_counter_1(control_unit_1_l_counter_1), .L_acc_0(control_unit_1_l_acc_0),
    .L_acc_2(control_unit_1_l_acc_2), .L_acc_1(control_unit_1_l_acc_1), .L_acc_3(control_unit_1_l_acc_3),
    .L_q0(control_unit_1_l_q0), .L_q1(control_unit_1_l_q1));
endmodule

module control_unit (
  input  clock,
  input  start,
  input  reset,
  input  l_bit_Q,
  input  Q_1,
  input  count__0,
  output L_acc_3,
  output L_q1,
  output L_counter_1,
  output L_q_1,
  output L_acc_1,
  output L_counter_0,
  output L_q0,
  output L_acc_0,
  output s_signal,
  output L_acc_2,
  output S_count,
  output S_q,
  output \end 
);

  wire cable, d_ff_1_q, d_ff_2_q, d_ff_5_q, demultiplexer_1_out0, demultiplexer_2_out0, demultiplexer_2_out1,
       demultiplexer_4_out0, demultiplexer_5_out0, demultiplexer_5_out1, or_1_out, or_2_out, or_3_out,
       or_4_out, xor_1_out;

  or or_1 (or_1_out, cable, demultiplexer_1_out0);
  D_Flip_Flop d_ff_1 (.clk(clock), .D(or_1_out), .Q(d_ff_1_q), .preset(reset));  // open: Qn, en, reset
  Demultiplexer #(.enable("false")) demultiplexer_1 (
    .out0(demultiplexer_1_out0), .out1(L_acc_0), .in(d_ff_1_q), .sel(start));
  D_Flip_Flop d_ff_2 (.clk(clock), .D(or_2_out), .Q(d_ff_2_q), .reset(reset));  // open: Qn, preset, en
  or or_2 (or_2_out, L_acc_0, demultiplexer_5_out0);
  Demultiplexer #(.enable("false")) demultiplexer_2 (
    .out0(demultiplexer_2_out0), .out1(demultiplexer_2_out1), .in(d_ff_2_q), .sel(xor_1_out));
  xor xor_1 (xor_1_out, l_bit_Q, Q_1);
  Demultiplexer #(.enable("false")) demultiplexer_3 (
    .out0(L_acc_1), .out1(L_acc_2), .in(demultiplexer_2_out1), .sel(l_bit_Q));
  or or_3 (or_3_out, demultiplexer_2_out0, L_acc_1, L_acc_2);
  D_Flip_Flop d_ff_3 (.clk(clock), .D(or_4_out), .Q(\end ), .reset(reset));  // open: Qn, preset, en
  or or_4 (or_4_out, demultiplexer_4_out0, demultiplexer_5_out1);
  Demultiplexer #(.enable("false")) demultiplexer_4 (
    .out0(demultiplexer_4_out0), .out1(cable), .in(\end ), .sel(start));
  D_Flip_Flop d_ff_4 (.clk(clock), .D(or_3_out), .Q(L_acc_3), .reset(reset));  // open: Qn, preset, en
  Demultiplexer #(.enable("false")) demultiplexer_5 (
    .out0(demultiplexer_5_out0), .out1(demultiplexer_5_out1), .in(d_ff_5_q), .sel(count__0));
  D_Flip_Flop d_ff_5 (.clk(clock), .D(L_acc_3), .Q(d_ff_5_q), .reset(reset));  // open: Qn, preset, en

  assign L_counter_0 = L_acc_0;
  assign L_counter_1 = L_acc_3;
  assign L_q0 = L_acc_0;
  assign L_q1 = L_acc_3;
  assign L_q_1 = L_acc_3;
  assign S_count = L_acc_3;
  assign S_q = L_acc_3;
  assign s_signal = L_acc_3;
endmodule

module data_path (
  input  s_signal,
  input  S_q,
  input  L_q_1,
  input  clock,
  input  reset,
  input  S_count,
  input  L_q0,
  input  L_q1,
  input  [3:0] multiplicand,
  input  [3:0] multiplier,
  input  L_counter_0,
  input  L_counter_1,
  input  L_acc_2,
  input  L_acc_3,
  input  L_acc_1,
  input  L_acc_0,
  output [7:0] result,
  output Q_1,
  output count__0,
  output l_bit_Q
);

  wire L_acc, L_counter, L_q;
  wire [1:0] S_acc;
  wire [2:0] count, count_1, multiplexer_3_out;
  wire [3:0] ACC_M, ACC_M_t, multiplexer_1_out, multiplexer_2_out;

  Multiplexer #(.select(2), .width(4), .enable("false")) multiplexer_1 (
    .in0({{2{result[7]}}, result[6:5]}), .in1(ACC_M), .in2(ACC_M_t), .in3({{2{result[7]}}, result[6:5]}),
    .out(multiplexer_1_out), .sel(S_acc));
  Register #(.width(4)) ACC (.D(multiplexer_1_out), .en(L_acc), .Q(result[7:4]), .clk(clock), .clr(reset));
  Multiplexer #(.width(4), .enable("false")) multiplexer_2 (
    .in0(multiplier), .in1(result[4:1]), .out(multiplexer_2_out), .sel(S_q));
  Register #(.width(4)) Q (.D(multiplexer_2_out), .en(L_q), .Q({result[3:1], l_bit_Q}), .clk(clock), .clr(reset));
  Multiplexer #(.width(3), .enable("false")) multiplexer_3 (
    .in0(3'b100), .in1(count_1), .out(multiplexer_3_out), .sel(S_count));
  Adder #(.width(4)) adder_1 (.a(result[7:4]), .b(multiplicand), .out(ACC_M));  // open: cin, cout
  Subtractor #(.width(4)) subtractor_1 (.a(result[7:4]), .b(multiplicand), .out(ACC_M_t));  // open: bin, bout
  D_Flip_Flop u_Q_1 (.clk(clock), .D(l_bit_Q), .Q(Q_1), .en(L_q_1), .reset(reset));  // open: Qn, preset
  Register #(.width(3)) register_1 (.D(multiplexer_3_out), .en(L_counter), .Q(count), .clk(clock));  // open: clr
  or or_1 (S_acc[0], Q_1, s_signal);
  or or_2 (S_acc[1], s_signal, l_bit_Q);
  or or_3 (L_counter, L_counter_0, L_counter_1);
  Subtractor #(.width(3)) subtractor_2 (.a(count), .b(3'b001), .out(count_1));  // open: bin, bout
  Comparator #(.width(3), .mode("unsigned")) comparator_1 (.a(count), .b(3'b000), .eq(count__0));  // open: gt, lt
  or or_4 (L_q, L_q0, L_q1);
  or or_5 (L_acc, L_acc_0, L_acc_2, L_acc_1, L_acc_3);

  assign result[0] = l_bit_Q;

  // Other names for the same wires on the sheet: Q[3:0] = {result[3:1], l_bit_Q}; ACC[3:0] = result[7:4];
  //   shift_s_acc[3:0] = {{2{result[7]}}, result[6:5]}; shift_s_q[3:0] = result[4:1]; l_bit_acc = result[4]
endmodule

module main (
  input  start,
  input  [3:0] B,
  input  [3:0] A,
  output \end ,
  output [7:0] result
);

  wire clock, reset;

  Clock clock_1 (.out(clock));
  Button button_1 (.out(reset));
  signed_multiplier signed_multiplier_1 (
    .clock(clock), .start(start), .reset(reset), .multiplicand(A), .multiplier(B), .result(result),
    .\end (\end ));

  // Other names for the same wires on the sheet: inputA[3:0] = A; inputB[3:0] = B
endmodule
