// Logisim project 1sImpares-0sPares.circ as structural Verilog: 1 circuit, main circuit main
module main (
  input  \output ,
  input  \input ,
  input  reset
);

  wire clock, not_1_out, s0, s1, s1_prime;

  xnor xnor_1 (s1_prime, s1, \input );
  and and_1 (\output , ~s1, s0);  // AND_Gate
  not not_1 (not_1_out, s0);
  Clock clock_1 (.out(clock));
  D_Flip_Flop d_ff_1 (.clk(clock), .D(s1_prime), .Q(s1), .en(1'b1), .reset(reset));  // open: Qn, preset
  D_Flip_Flop d_ff_2 (.clk(clock), .D(not_1_out), .Q(s0), .en(1'b1), .reset(reset));  // open: Qn, preset
endmodule
