// Logisim project altern_input.circ as structural Verilog: 1 circuit, main circuit main
module main (
  input  \input ,
  input  reset,
  output out_3
);

  wire clock_1_out, d_ff_1_q, not_1_out;

  Clock clock_1 (.out(clock_1_out));
  not not_1 (not_1_out, d_ff_1_q);
  D_Flip_Flop d_ff_1 (.clk(clock_1_out), .D(not_1_out), .Q(d_ff_1_q), .en(1'b1), .reset(reset));  // open: Qn, preset
  xnor xnor_1 (out_3, \input , d_ff_1_q);
endmodule
