// Logisim project patron_1101.circ as structural Verilog: 2 circuits, main circuit generar_patron
module generar_patron (
  input  reset,
  output pattern,
  output out_3
);

  wire clock, not_1_out, s0, s1, xor_1_out;

  Clock clock_1 (.out(clock));
  xor xor_1 (xor_1_out, s1, s0);
  not not_1 (not_1_out, s0);
  D_Flip_Flop d_ff_1 (.clk(clock), .D(xor_1_out), .Q(s1), .en(1'b1), .reset(reset));  // open: Qn, preset
  D_Flip_Flop d_ff_2 (.clk(clock), .D(not_1_out), .Q(s0), .en(1'b1), .reset(reset));  // open: Qn, preset
  or or_1 (pattern, s1, ~s0);  // OR_Gate
  check_patron check_patron_1 (.\input (pattern), .reset(reset), .\output (out_3), .in_2(clock));

  // Notes on the sheet:
  //   Output Logic
endmodule

module check_patron (
  input  \input ,
  input  in_2,
  input  reset,
  output \output 
);

  wire and_3_out, and_4_out, not_1_out, or_1_out, or_2_out, s0, s0_prime, s1, s1_prime, s2_prime;

  and and_1 (s0_prime, \input , or_1_out);
  or or_1 (or_1_out, ~s0, ~s1);  // OR_Gate
  and and_2 (s2_prime, s0, s1, ~\output , \input );  // AND_Gate
  and and_3 (and_3_out, ~s0, s1, \input );  // AND_Gate
  and and_4 (and_4_out, ~\input , s0);  // AND_Gate
  not not_1 (not_1_out, \output );
  or or_2 (or_2_out, and_3_out, and_4_out);
  and and_5 (s1_prime, not_1_out, or_2_out);
  D_Flip_Flop d_ff_1 (.clk(in_2), .D(s2_prime), .Q(\output ), .en(1'b1), .reset(reset));  // open: Qn, preset
  D_Flip_Flop d_ff_2 (.clk(in_2), .D(s1_prime), .Q(s1), .en(1'b1), .reset(reset));  // open: Qn, preset
  D_Flip_Flop d_ff_3 (.clk(in_2), .D(s0_prime), .Q(s0), .en(1'b1), .reset(reset));  // open: Qn, preset

  // Other names for the same wires on the sheet: clock = in_2; s2 = \output 
endmodule
