// Logisim project flip_flops.circ as structural Verilog: 8 circuits, main circuit weird_behaviour_race
module weird_behaviour_race (
  input  in_1,
  input  in_2,
  output out_3
);

  wire and_1_out, not_1_out;

  and and_1 (and_1_out, in_1, not_1_out);
  not not_1 (not_1_out, in_1);
  D_Flip_Flop d_ff_1 (.clk(and_1_out), .D(1'b1), .Q(out_3), .reset(in_2));  // open: Qn, preset, en

  // Notes on the sheet:
  //   Weird Situation
  //   Allows a circuit that initially is in a stable state, and after a signal alterns its input forever
endmodule

module set_reset_v1 (
  input  value_to_latch,
  input  reset,
  output Q1
);

  wire or_1_out;

  or or_1 (or_1_out, Q1, value_to_latch);
  and and_1 (Q1, or_1_out, ~reset);  // AND_Gate

  // Other names for the same wires on the sheet: set = value_to_latch
endmodule

module set_reset_v2 (
  input  value_to_latch,
  input  reset,
  output Q2
);

  wire nor_1_out;

  nor nor_1 (nor_1_out, value_to_latch, Q2);
  nor nor_2 (Q2, nor_1_out, reset);

  // Other names for the same wires on the sheet: set = value_to_latch
endmodule

module D_Latch (
  input  preset,
  input  D,
  input  enable,
  input  reset,
  output Q
);

  wire and_1_out, and_2_out, or_1_out, or_2_out;

  and and_1 (and_1_out, D, enable);
  and and_2 (and_2_out, enable, ~D);  // AND_Gate
  or or_1 (or_1_out, preset, and_1_out);
  or or_2 (or_2_out, and_2_out, reset);
  set_reset_v1 set_reset_v1_1 (.value_to_latch(or_1_out), .reset(or_2_out), .Q1(Q));
endmodule

module D_flip_flop (
  input  D,
  input  clock,
  input  enable,
  input  asyn_preset,
  input  asyn_clear,
  output Q
);

  wire and_1_out, d_latch_master_q, not_1_out;

  not not_1 (not_1_out, clock);
  and and_1 (and_1_out, clock, enable);
  D_Latch d_latch_master (.D(D), .enable(not_1_out), .Q(d_latch_master_q), .reset(asyn_clear), .preset(asyn_preset));
  D_Latch d_latch_slave (.D(d_latch_master_q), .enable(and_1_out), .Q(Q), .reset(asyn_clear), .preset(asyn_preset));
endmodule

module T_flip_flop (
  input  toogle,
  input  clock,
  input  enable,
  input  asyn_preset,
  input  asyn_clear,
  output Q
);

  wire and_1_out, master_q, not_1_out, xor_1_out;

  not not_1 (not_1_out, clock);
  xor xor_1 (xor_1_out, Q, toogle);
  and and_1 (and_1_out, clock, enable);
  D_Latch master (.D(xor_1_out), .enable(not_1_out), .Q(master_q), .reset(asyn_clear), .preset(asyn_preset));
  D_Latch slave (.D(master_q), .enable(and_1_out), .Q(Q), .reset(asyn_clear), .preset(asyn_preset));
endmodule

module SR_Flip_Flop (
  input  set,
  input  reset,
  input  clock,
  input  asyn_preset,
  input  asyn_clear,
  input  enable,
  output Q
);

  wire and_1_out, master_q, not_1_out, set_reset_logic_q1;

  set_reset_v1 set_reset_logic (.value_to_latch(set), .reset(reset), .Q1(set_reset_logic_q1));
  not not_1 (not_1_out, clock);
  D_Latch master (.D(set_reset_logic_q1), .enable(not_1_out), .Q(master_q), .reset(asyn_clear), .preset(asyn_preset));
  and and_1 (and_1_out, clock, enable);
  D_Latch slave (.D(master_q), .enable(and_1_out), .Q(Q), .reset(asyn_clear), .preset(asyn_preset));
endmodule

module JK_Flip_Flop (
  input  J,
  input  K,
  input  clock,
  input  asyn_preset,
  input  asyn_clear,
  input  enable,
  output Q
);

  wire and_1_out, master_q, multiplexer_1_out, not_1_out, not_2_out, set_reset_v1_1_q1;

  set_reset_v1 set_reset_v1_1 (.value_to_latch(J), .reset(K), .Q1(set_reset_v1_1_q1));
  Multiplexer #(.select(2), .enable("false")) multiplexer_1 (
    .in0(Q), .in1(set_reset_v1_1_q1), .in2(set_reset_v1_1_q1), .in3(not_1_out), .out(multiplexer_1_out),
    .sel({K, J}));
  not not_1 (not_1_out, Q);
  not not_2 (not_2_out, clock);
  D_Latch master (.D(multiplexer_1_out), .enable(not_2_out), .Q(master_q), .reset(asyn_clear), .preset(asyn_preset));
  and and_1 (and_1_out, clock, enable);
  D_Latch slave (.D(master_q), .enable(and_1_out), .Q(Q), .reset(asyn_clear), .preset(asyn_preset));
endmodule
