// Logisim project parallel_multiplier.circ as structural Verilog: 5 circuits, main circuit parallel_multiplier
module parallel_multiplier (
  input  [3:0] multiplicand,
  input  [3:0] multiplier,
  input  clock,
  input  start,
  input  a_reset,
  output [8:0] result,
  output Done
);

  wire add, adder_1_cout, b0, b1, b2, b3, b4, b5, b6, b7, carry, K, load, load_selector, s0, s1, s2, s3,
       shift_signal;
  wire [3:0] multiplexer_2_out, multiplexer_3_out;
  wire [8:0] multiplexer_1_out;

  Multiplexer #(.width(9), .enable("false")) multiplexer_1 (
    .in0({{5{1'b0}}, multiplier}), .in1({carry, s3, s2, s1, s0, b3, b2, b1, b0}), .out(multiplexer_1_out),
    .sel(load_selector));
  _2_bit_counter u_2_bit_counter_1 (.clock(clock), .\input (shift_signal), .K(K));  // open: reset
  right_shift_register right_shift_register_1 (
    .shift_right(shift_signal), .clock(clock), .load(load), .serial_input(1'b0), .asyncronous_reset(a_reset),
    .parallel_input(multiplexer_1_out), .whole_vaue(result), .b7(b7), .b6(b6), .b5(b5), .b4(b4), .b3(b3),
    .b2(b2), .b1(b1), .b0(b0));
  add_shift_control add_shift_control_1 (
    .K(K), .start(start), .M(b0), .clock(clock), .a_reset(a_reset), .done(Done),
    .load_selector(load_selector), .load(load), .add(add), .sh(shift_signal));
  Multiplexer #(.width(4), .enable("false")) multiplexer_2 (
    .in0(4'b0000), .in1({b7, b6, b5, b4}), .out(multiplexer_2_out), .sel(add));
  Multiplexer #(.width(4), .enable("false")) multiplexer_3 (
    .in0({b7, b6, b5, b4}), .in1(multiplicand), .out(multiplexer_3_out), .sel(add));
  Adder #(.width(4)) adder_1 (
    .a(multiplexer_2_out), .b(multiplexer_3_out), .out({s3, s2, s1, s0}), .cout(adder_1_cout));  // open: cin
  Multiplexer #(.enable("false")) multiplexer_4 (.in0(1'b0), .in1(adder_1_cout), .out(carry), .sel(add));

  // Other names for the same wires on the sheet: M = b0
endmodule

module _2_bit_counter (
  input  reset,
  input  clock,
  input  \input ,
  output K
);

  wire and_1_out, t_ff_1_q, t_ff_2_q;

  T_Flip_Flop t_ff_1 (.clk(clock), .T(and_1_out), .Q(t_ff_1_q), .reset(reset));  // open: Qn, preset, en
  and and_1 (and_1_out, \input , t_ff_2_q);
  and and_2 (K, t_ff_1_q, t_ff_2_q);
  T_Flip_Flop t_ff_2 (.clk(clock), .T(\input ), .Q(t_ff_2_q), .reset(reset));  // open: Qn, preset, en
endmodule

module right_shift_register (
  input  shift_right,
  input  clock,
  input  load,
  input  serial_input,
  input  asyncronous_reset,
  input  [8:0] parallel_input,
  output [8:0] whole_vaue,
  output b5,
  output b3,
  output b1,
  output b7,
  output b4,
  output b6,
  output b2,
  output b0
);

  wire multiplexer_1_out, multiplexer_2_out, multiplexer_3_out, multiplexer_4_out, multiplexer_5_out,
       multiplexer_6_out, multiplexer_7_out, multiplexer_8_out, multiplexer_9_out;

  D_Flip_Flop d_ff_1 (
    .clk(clock), .D(multiplexer_1_out), .Q(whole_vaue[8]), .reset(asyncronous_reset));  // open: Qn, preset, en
  Multiplexer #(.select(2), .enable("false")) multiplexer_1 (
    .in0(whole_vaue[8]), .in1(serial_input), .in2(parallel_input[8]), .in3(parallel_input[8]),
    .out(multiplexer_1_out), .sel({load, shift_right}));
  Multiplexer #(.select(2), .enable("false")) multiplexer_2 (
    .in0(b7), .in1(whole_vaue[8]), .in2(parallel_input[7]), .in3(parallel_input[7]), .out(multiplexer_2_out),
    .sel({load, shift_right}));
  D_Flip_Flop d_ff_2 (.clk(clock), .D(multiplexer_2_out), .Q(b7), .reset(asyncronous_reset));  // open: Qn, preset, en
  Multiplexer #(.select(2), .enable("false")) multiplexer_3 (
    .in0(b6), .in1(b7), .in2(parallel_input[6]), .in3(parallel_input[6]), .out(multiplexer_3_out),
    .sel({load, shift_right}));
  D_Flip_Flop d_ff_3 (.clk(clock), .D(multiplexer_3_out), .Q(b6), .reset(asyncronous_reset));  // open: Qn, preset, en
  Multiplexer #(.select(2), .enable("false")) multiplexer_4 (
    .in0(b5), .in1(b6), .in2(parallel_input[5]), .in3(parallel_input[5]), .out(multiplexer_4_out),
    .sel({load, shift_right}));
  D_Flip_Flop d_ff_4 (.clk(clock), .D(multiplexer_4_out), .Q(b5), .reset(asyncronous_reset));  // open: Qn, preset, en
  Multiplexer #(.select(2), .enable("false")) multiplexer_5 (
    .in0(b4), .in1(b5), .in2(parallel_input[4]), .in3(parallel_input[4]), .out(multiplexer_5_out),
    .sel({load, shift_right}));
  D_Flip_Flop d_ff_5 (.clk(clock), .D(multiplexer_5_out), .Q(b4), .reset(asyncronous_reset));  // open: Qn, preset, en
  D_Flip_Flop d_ff_6 (.clk(clock), .D(multiplexer_6_out), .Q(b3), .reset(asyncronous_reset));  // open: Qn, preset, en
  Multiplexer #(.select(2), .enable("false")) multiplexer_6 (
    .in0(b3), .in1(b4), .in2(parallel_input[3]), .in3(parallel_input[3]), .out(multiplexer_6_out),
    .sel({load, shift_right}));
  Multiplexer #(.select(2), .enable("false")) multiplexer_7 (
    .in0(b2), .in1(b3), .in2(parallel_input[2]), .in3(parallel_input[2]), .out(multiplexer_7_out),
    .sel({load, shift_right}));
  D_Flip_Flop d_ff_7 (.clk(clock), .D(multiplexer_7_out), .Q(b2), .reset(asyncronous_reset));  // open: Qn, preset, en
  Multiplexer #(.select(2), .enable("false")) multiplexer_8 (
    .in0(b1), .in1(b2), .in2(parallel_input[1]), .in3(parallel_input[1]), .out(multiplexer_8_out),
    .sel({load, shift_right}));
  D_Flip_Flop d_ff_8 (.clk(clock), .D(multiplexer_8_out), .Q(b1), .reset(asyncronous_reset));  // open: Qn, preset, en
  Multiplexer #(.select(2), .enable("false")) multiplexer_9 (
    .in0(b0), .in1(b1), .in2(parallel_input[0]), .in3(parallel_input[0]), .out(multiplexer_9_out),
    .sel({load, shift_right}));
  D_Flip_Flop d_ff_9 (.clk(clock), .D(multiplexer_9_out), .Q(b0), .reset(asyncronous_reset));  // open: Qn, preset, en

  assign whole_vaue[7:0] = {b7, b6, b5, b4, b3, b2, b1, b0};

  // Other names for the same wires on the sheet: a_reset = asyncronous_reset; clk = clock; l0 = parallel_input[0];
  //   l1 = parallel_input[1]; l2 = parallel_input[2]; l3 = parallel_input[3]; l4 = parallel_input[4];
  //   l5 = parallel_input[5]; l6 = parallel_input[6]; l7 = parallel_input[7]; l8 = parallel_input[8];
  //   S[1:0] = {load, shift_right}; sr = shift_right; ld = load; si = serial_input; b8 = whole_vaue[8]
endmodule

module main (
  input  [3:0] multiplicand,
  input  [3:0] multiplier,
  input  start,
  input  a_reset,
  output [8:0] out_5,
  output \output 
);

  wire clock_out;

  Clock clock (.out(clock_out));
  parallel_multiplier parallel_multiplier_1 (
    .multiplicand(multiplicand), .multiplier(multiplier), .clock(clock_out), .start(start),
    .a_reset(a_reset), .result(out_5), .Done(\output ));
endmodule

module add_shift_control (
  input  K,
  input  start,
  input  M,
  input  clock,
  input  a_reset,
  output done,
  output load_selector,
  output load,
  output add,
  output sh
);

  wire and_2_out, and_3_out, and_4_out, and_5_out, and_6_out, and_8_out, and_9_out, and_10_out, and_11_out,
       b0, b0_prime, b1, b1_prime, or_1_out;

  and and_1 (add, b0, ~b1, M);  // AND_Gate
  D_Flip_Flop d_ff_1 (.clk(clock), .D(b0_prime), .Q(b0), .reset(a_reset));  // open: Qn, preset, en
  D_Flip_Flop d_ff_2 (.clk(clock), .D(b1_prime), .Q(b1), .reset(a_reset));  // open: Qn, preset, en
  and and_2 (and_2_out, b0, ~b1, ~M);  // AND_Gate
  or or_1 (or_1_out, K, M);
  and and_3 (and_3_out, start, ~b1, ~b0);  // AND_Gate
  and and_4 (and_4_out, or_1_out, b1, ~b0);  // AND_Gate
  and and_5 (and_5_out, M, ~b1, b0);  // AND_Gate
  and and_6 (and_6_out, ~b1, ~b0, start);  // AND_Gate
  or or_2 (b0_prime, and_3_out, and_2_out, and_4_out);
  or or_3 (load_selector, b0, b1);
  or or_4 (load, and_5_out, and_6_out);
  and and_7 (done, b0, b1);
  and and_8 (and_8_out, b0, ~b1, M);  // AND_Gate
  and and_9 (and_9_out, b0, ~b1, ~M);  // AND_Gate
  and and_10 (and_10_out, b1, ~b0, ~M);  // AND_Gate
  and and_11 (and_11_out, ~b0, b1);  // AND_Gate
  or or_5 (sh, and_11_out, and_9_out);
  or or_6 (b1_prime, and_10_out, and_8_out, K);
endmodule
