// Logisim project ram.circ as structural Verilog: 3 circuits, main circuit three_bit_address_ram
module three_bit_address_ram (
  input  [7:0] in_1,
  input  [2:0] address,
  input  read_write,
  input  clock,
  input  clear,
  output [7:0] load_store_data
);

  wire and_1_out, and_2_out, and_3_out, and_4_out, and_5_out, and_6_out, and_7_out, and_8_out, and_9_out,
       and_10_out, and_11_out, and_12_out, and_13_out, and_14_out, and_15_out, and_16_out, decoder_1_out0,
       decoder_1_out1, decoder_1_out2, decoder_1_out3, decoder_1_out4, decoder_1_out5, decoder_1_out6,
       decoder_1_out7;
  wire [7:0] register_1_q, register_2_q, register_3_q, register_4_q, register_5_q, register_6_q,
       register_7_q, register_8_q;

  Decoder #(.select(3), .enable("false")) decoder_1 (
    .out0(decoder_1_out0), .out1(decoder_1_out1), .out2(decoder_1_out2), .out3(decoder_1_out3),
    .out4(decoder_1_out4), .out5(decoder_1_out5), .out6(decoder_1_out6), .out7(decoder_1_out7), .sel(address));
  and and_1 (and_1_out, read_write, decoder_1_out0);
  and and_2 (and_2_out, ~read_write, decoder_1_out0);  // AND_Gate
  and and_3 (and_3_out, read_write, decoder_1_out1);
  and and_4 (and_4_out, ~read_write, decoder_1_out1);  // AND_Gate
  and and_5 (and_5_out, read_write, decoder_1_out2);
  and and_6 (and_6_out, ~read_write, decoder_1_out2);  // AND_Gate
  and and_7 (and_7_out, read_write, decoder_1_out3);
  and and_8 (and_8_out, ~read_write, decoder_1_out3);  // AND_Gate
  and and_9 (and_9_out, read_write, decoder_1_out4);
  and and_10 (and_10_out, ~read_write, decoder_1_out4);  // AND_Gate
  and and_11 (and_11_out, read_write, decoder_1_out5);
  and and_12 (and_12_out, ~read_write, decoder_1_out5);  // AND_Gate
  and and_13 (and_13_out, read_write, decoder_1_out6);
  and and_14 (and_14_out, ~read_write, decoder_1_out6);  // AND_Gate
  and and_15 (and_15_out, ~read_write, decoder_1_out7);  // AND_Gate
  and and_16 (and_16_out, read_write, decoder_1_out7);
  Register register_1 (.D(load_store_data), .en(and_1_out), .Q(register_1_q), .clk(clock), .clr(clear));
  Register register_2 (.D(load_store_data), .en(and_3_out), .Q(register_2_q), .clk(clock), .clr(clear));
  Register register_3 (.D(load_store_data), .en(and_5_out), .Q(register_3_q), .clk(clock), .clr(clear));
  Register register_4 (.D(load_store_data), .en(and_7_out), .Q(register_4_q), .clk(clock), .clr(clear));
  Register register_5 (.D(load_store_data), .en(and_9_out), .Q(register_5_q), .clk(clock), .clr(clear));
  Register register_6 (.D(load_store_data), .en(and_11_out), .Q(register_6_q), .clk(clock), .clr(clear));
  Register register_7 (.D(load_store_data), .en(and_13_out), .Q(register_7_q), .clk(clock), .clr(clear));
  Register register_8 (.D(load_store_data), .en(and_15_out), .Q(register_8_q), .clk(clock), .clr(clear));
  assign load_store_data = and_2_out ? register_1_q : 8'bz;  // Controlled_Buffer controlled_buffer_1
  assign load_store_data = and_4_out ? register_2_q : 8'bz;  // Controlled_Buffer controlled_buffer_2
  assign load_store_data = and_6_out ? register_3_q : 8'bz;  // Controlled_Buffer controlled_buffer_3
  assign load_store_data = and_8_out ? register_4_q : 8'bz;  // Controlled_Buffer controlled_buffer_4
  assign load_store_data = and_10_out ? register_5_q : 8'bz;  // Controlled_Buffer controlled_buffer_5
  assign load_store_data = and_12_out ? register_6_q : 8'bz;  // Controlled_Buffer controlled_buffer_6
  assign load_store_data = and_14_out ? register_7_q : 8'bz;  // Controlled_Buffer controlled_buffer_7
  assign load_store_data = and_16_out ? register_8_q : 8'bz;  // Controlled_Buffer controlled_buffer_8
  assign load_store_data = read_write ? in_1 : 8'bz;  // Controlled_Buffer controlled_buffer_9

  // Other names for the same wires on the sheet: reset = clear

  // Notes on the sheet:
  //   3-bit Address 1 Byte Addressable RAM
endmodule

module main (
  input  [7:0] store_data,
  input  write,
  input  [2:0] Address,
  output [7:0] load_store_data
);

  wire clock_out, not_1_out;

  assign load_store_data = write ? store_data : 8'bz;  // Controlled_Buffer controlled_buffer_1
  not not_1 (not_1_out, write);
  Clock clock (.out(clock_out));
  RAM #(.addrWidth(3)) ram_1 (
    .addr(Address), .data(load_store_data), .clk(clock_out), .ld(not_1_out));  // open: sel, clr
endmodule

module ram_with_teletype_keyboard (
  input  in_1,
  input  in_2
);

  wire altern_read_write_out, button_1_out, button_2_out, rd, wrt;
  wire [6:0] controlled_buffer_2_out, keyboard_1_data, ram_1_data;
  wire [7:0] counter_1_q;

  Button altern_read_write (.out(altern_read_write_out));
  T_Flip_Flop t_ff_1 (.clk(altern_read_write_out), .T(1'b1), .Q(wrt), .Qn(rd));  // open: preset, reset, en
  Counter counter_1 (.Q(counter_1_q), .clk(in_1), .clr(button_1_out));  // open: load, D, count, carry
  Button button_1 (.out(button_1_out));
  Keyboard keyboard_1 (.clk(in_1), .re(wrt), .clr(button_2_out), .data(keyboard_1_data));  // open: avail
  Button button_2 (.out(button_2_out));
  RAM #(.dataWidth(7)) ram_1 (.addr(counter_1_q), .data(ram_1_data), .clk(in_1), .ld(rd));  // open: sel, clr
  assign ram_1_data = wrt ? keyboard_1_data : 7'bz;  // Controlled_Buffer controlled_buffer_1
  assign controlled_buffer_2_out = rd ? ram_1_data : 7'bz;  // Controlled_Buffer controlled_buffer_2
  TTY #(.cols(25)) tty_1 (.data(controlled_buffer_2_out), .clk(in_1), .we(rd), .clr(in_2));

  // Other names for the same wires on the sheet: clock = in_1; reset = in_2
endmodule
