// Logisim project serial_adder.circ as structural Verilog: 4 circuits, main circuit right_shift_register_parllel_serial_input_
module main (
  input  load,
  input  [3:0] in_2,
  input  [3:0] in_3,
  input  start,
  output [3:0] out_5
);

  wire clock_1_out;

  Clock clock_1 (.out(clock_1_out));
  adder_serie adder_serie_1 (.load(load), .clock(clock_1_out), .in_3(start), .inputB(in_2), .inputA(in_3), .sum(out_5));
endmodule

module right_shift_register_parllel_serial_input (
  input  shift_right,
  input  load,
  input  asyncronous_reset,
  input  clock,
  input  serial_input,
  input  [3:0] parallel_input,
  output [3:0] whole_value,
  output last_bit
);

  wire multiplexer_1_out, multiplexer_2_out, multiplexer_3_out, multiplexer_4_out;

  Multiplexer #(.select(2), .enable("false")) multiplexer_1 (
    .in0(whole_value[3]), .in1(serial_input), .in2(parallel_input[3]), .in3(parallel_input[3]),
    .out(multiplexer_1_out), .sel({load, shift_right}));
  D_Flip_Flop d_ff_1 (
    .clk(clock), .D(multiplexer_1_out), .Q(whole_value[3]), .reset(asyncronous_reset));  // open: Qn, preset, en
  Multiplexer #(.select(2), .enable("false")) multiplexer_2 (
    .in0(whole_value[2]), .in1(whole_value[3]), .in2(parallel_input[2]), .in3(parallel_input[2]),
    .out(multiplexer_2_out), .sel({load, shift_right}));
  D_Flip_Flop d_ff_2 (
    .clk(clock), .D(multiplexer_2_out), .Q(whole_value[2]), .reset(asyncronous_reset));  // open: Qn, preset, en
  Multiplexer #(.select(2), .enable("false")) multiplexer_3 (
    .in0(whole_value[1]), .in1(whole_value[2]), .in2(parallel_input[1]), .in3(parallel_input[1]),
    .out(multiplexer_3_out), .sel({load, shift_right}));
  D_Flip_Flop d_ff_3 (
    .clk(clock), .D(multiplexer_3_out), .Q(whole_value[1]), .reset(asyncronous_reset));  // open: Qn, preset, en
  Multiplexer #(.select(2), .enable("false")) multiplexer_4 (
    .in0(last_bit), .in1(whole_value[1]), .in2(parallel_input[0]), .in3(parallel_input[0]),
    .out(multiplexer_4_out), .sel({load, shift_right}));
  D_Flip_Flop d_ff_4 (
    .clk(clock), .D(multiplexer_4_out), .Q(last_bit), .reset(asyncronous_reset));  // open: Qn, preset, en

  assign whole_value[0] = last_bit;

  // Other names for the same wires on the sheet: a_reset = asyncronous_reset; clk = clock; l0 = parallel_input[0];
  //   l1 = parallel_input[1]; l2 = parallel_input[2]; l3 = parallel_input[3]; S[1:0] = {load, shift_right};
  //   sr = shift_right; ld = load; si = serial_input; b0 = last_bit; b1 = whole_value[1]; b2 = whole_value[2];
  //   b3 = whole_value[3]
endmodule

module adder_serie (
  input  load,
  input  clock,
  input  in_3,
  input  [3:0] inputB,
  input  [3:0] inputA,
  output [3:0] sum
);

  wire adder_1_cout, clear, d_ff_1_q, right_shift_register_parllel_serial_input_1_last_bit,
       right_shift_register_parllel_serial_input_2_last_bit, shift_signal, si;

  fsm_01111 fsm_01111_1 (.clock(clock), .\input (in_3), .\output (shift_signal), .clear(clear));
  right_shift_register_parllel_serial_input right_shift_register_parllel_serial_input_1 (
    .shift_right(shift_signal), .load(load), .clock(clock), .serial_input(si),
    .last_bit(right_shift_register_parllel_serial_input_1_last_bit), .whole_value(sum),
    .parallel_input(inputB));  // open: asyncronous_reset
  right_shift_register_parllel_serial_input right_shift_register_parllel_serial_input_2 (
    .shift_right(shift_signal), .load(load), .clock(clock),
    .serial_input(right_shift_register_parllel_serial_input_2_last_bit),
    .last_bit(right_shift_register_parllel_serial_input_2_last_bit), .parallel_input(inputA));  // open: whole_value, asyncronous_reset
  Adder #(.width(1)) adder_1 (
    .a(right_shift_register_parllel_serial_input_1_last_bit),
    .b(right_shift_register_parllel_serial_input_2_last_bit), .out(si), .cin(d_ff_1_q), .cout(adder_1_cout));
  D_Flip_Flop d_ff_1 (
    .clk(clock), .D(adder_1_cout), .Q(d_ff_1_q), .en(shift_signal), .reset(clear));  // open: Qn, preset

  // Other names for the same wires on the sheet: clk = clock; l = load; start = in_3
endmodule

module fsm_01111 (
  input  clock,
  input  \input ,
  output clear,
  output \output 
);

  wire a_bit0, a_bit1, and_2_out, and_3_out, and_4_out, and_5_out, bit0, bit1, not_1_out, not_2_out,
       not_3_out, not_4_out;

  D_Flip_Flop d_ff_1 (.clk(clock), .D(a_bit1), .Q(bit1));  // open: Qn, preset, en, reset
  D_Flip_Flop d_ff_2 (.clk(clock), .D(a_bit0), .Q(bit0));  // open: Qn, preset, en, reset
  and and_1 (clear, ~bit0, ~bit1);  // AND_Gate
  or or_1 (\output , bit1, bit0, \input );
  not not_1 (not_1_out, bit0);
  not not_2 (not_2_out, bit0);
  not not_3 (not_3_out, bit0);
  not not_4 (not_4_out, bit1);
  and and_2 (and_2_out, not_1_out, bit1);
  and and_3 (and_3_out, \input , not_2_out);
  and and_4 (and_4_out, not_3_out, bit1);
  and and_5 (and_5_out, bit0, not_4_out);
  or or_2 (a_bit0, and_2_out, and_3_out);
  or or_3 (a_bit1, and_4_out, and_5_out);

  // Other names for the same wires on the sheet: clk = clock
endmodule
