// Logisim project fsamcd.circ as structural Verilog: 2 circuits, main circuit mcd
module mcd (
  input  [7:0] a,
  input  [7:0] b,
  input  clock,
  input  reset,
  input  start,
  output [7:0] \output ,
  output out_7
);

  wire A___B, A_nB, comparator_1_eq, d_ff_1_q, demultiplexer_1_out0, demultiplexer_2_out0,
       demultiplexer_2_out1, demultiplexer_3_out0, demultiplexer_4_out0, demultiplexer_4_out1, idle_q, LA,
       LA0, LA1, LB, LB2, or_3_out, or_4_out, or_5_out, or_6_out, or_7_out;
  wire [7:0] B_A, B_t, multiplexer_1_out, multiplexer_2_out;

  Multiplexer #(.width(8), .enable("false")) multiplexer_1 (.in0(a), .in1(B_t), .out(multiplexer_1_out), .sel(LA1));
  Register register_1 (.D(multiplexer_1_out), .en(LA), .Q(\output ), .clk(clock), .clr(reset));
  or or_1 (LB, LA0, LA1, LB2);
  or or_2 (LA, LA0, LA1);
  D_Flip_Flop idle (.clk(clock), .D(or_4_out), .Q(idle_q), .preset(or_3_out), .en(1'b1));  // open: Qn, reset
  or or_3 (or_3_out, start, reset);
  or or_4 (or_4_out, demultiplexer_4_out1, demultiplexer_1_out0);
  Demultiplexer #(.enable("false")) demultiplexer_1 (.out0(demultiplexer_1_out0), .out1(LA0), .in(idle_q), .sel(start));
  Multiplexer #(.select(2), .width(8), .enable("false")) multiplexer_2 (
    .in0(b), .in1(\output ), .in2(B_A), .out(multiplexer_2_out), .sel({LB2, LA1}));  // open: in3
  or or_5 (or_5_out, LA0, LB2);
  Register register_2 (.D(multiplexer_2_out), .en(LB), .Q(B_t), .clk(clock), .clr(reset));
  D_Flip_Flop d_ff_1 (.clk(clock), .D(or_5_out), .Q(d_ff_1_q), .en(1'b1), .reset(reset));  // open: Qn, preset
  Demultiplexer #(.enable("false")) demultiplexer_2 (
    .out0(demultiplexer_2_out0), .out1(demultiplexer_2_out1), .in(d_ff_1_q), .sel(A_nB));
  Subtractor subtractor_1 (.a(B_t), .b(\output ), .out(B_A));  // open: bin, bout
  Comparator comparator_1 (.a(\output ), .b(B_t), .gt(A___B), .eq(comparator_1_eq));  // open: lt
  or or_6 (or_6_out, demultiplexer_4_out0, demultiplexer_2_out0);
  Demultiplexer #(.enable("false")) demultiplexer_3 (
    .out0(demultiplexer_3_out0), .out1(LA1), .in(demultiplexer_2_out1), .sel(A___B));
  not not_1 (A_nB, comparator_1_eq);
  D_Flip_Flop \end  (.clk(clock), .D(or_6_out), .Q(out_7), .en(1'b1), .reset(reset));  // open: Qn, preset
  Demultiplexer #(.enable("false")) demultiplexer_4 (
    .out0(demultiplexer_4_out0), .out1(demultiplexer_4_out1), .in(out_7), .sel(start));
  or or_7 (or_7_out, demultiplexer_3_out0, LA1);
  D_Flip_Flop after_if (.clk(clock), .D(or_7_out), .Q(LB2), .en(1'b1), .reset(reset));  // open: Qn, preset

  // Other names for the same wires on the sheet: A_t[7:0] = \output ; LB0 = LA0; LB1 = LA1; SA = LA1;
  //   SB[1:0] = {LB2, LA1}; SB0 = LA1; SB1 = LB2
endmodule

module main (
  input  [7:0] a,
  input  [7:0] b,
  input  reset,
  input  start,
  output [7:0] out_5,
  output out_6
);

  wire clock_1_out;

  Clock clock_1 (.out(clock_1_out));
  mcd mcd_1 (.a(a), .b(b), .clock(clock_1_out), .reset(reset), .start(start), .\output (out_5), .out_7(out_6));
endmodule
