// Logisim project marie01.circ as structural Verilog: 1 circuit, main circuit marie0.1
module marie0_1 (
  input  start,
  input  reset,
  input  clock,
  output [15:0] out_4
);

  wire comparator_1_eq, demultiplexer_1_out0, demultiplexer_1_out1, demultiplexer_2_out0, e_IR, idle_q,
       no_stop, or_1_out, or_2_out, or_3_out, or_4_out, r_ram, step1_q, step3_q;
  wire [11:0] PC, PC_1;
  wire [15:0] IR;

  or or_1 (or_1_out, demultiplexer_2_out0, demultiplexer_1_out0);
  D_Flip_Flop idle (.clk(clock), .D(or_1_out), .Q(idle_q), .preset(reset));  // open: Qn, en, reset
  Demultiplexer #(.enable("false")) demultiplexer_1 (
    .out0(demultiplexer_1_out0), .out1(demultiplexer_1_out1), .in(idle_q), .sel(start));
  Comparator #(.width(4), .mode("unsigned")) comparator_1 (
    .a(IR[15:12]), .b(4'b1111), .eq(comparator_1_eq));  // open: gt, lt
  Adder #(.width(12)) adder_1 (.a(PC), .b(12'h1), .out(PC_1));  // open: cin, cout
  or or_2 (or_2_out, demultiplexer_1_out1, step3_q);
  not not_1 (no_stop, comparator_1_eq);
  Demultiplexer #(.enable("false")) demultiplexer_2 (
    .out0(demultiplexer_2_out0), .out1(r_ram), .in(step1_q), .sel(no_stop));
  D_Flip_Flop step1 (.clk(clock), .D(or_2_out), .Q(step1_q), .reset(reset));  // open: Qn, preset, en
  RAM #(.addrWidth(12), .dataWidth(16), .bus("separate")) ram_1 (
    .addr(PC), .data(out_4), .str(1'b0), .clk(clock), .ld(1'b1));  // open: din, sel, clr
  or or_3 (or_3_out, r_ram, 1'b0);
  Register #(.width(16)) u_IR (.D(out_4), .en(e_IR), .Q(IR), .clk(clock), .clr(reset));
  D_Flip_Flop step2 (.clk(clock), .D(or_3_out), .Q(e_IR), .reset(reset));  // open: Qn, preset, en
  Register #(.width(12)) u_PC (.D(PC_1), .en(e_IR), .Q(PC), .clk(clock), .clr(reset));
  or or_4 (or_4_out, e_IR, 1'b0);
  D_Flip_Flop step3 (.clk(clock), .D(or_4_out), .Q(step3_q), .reset(reset));  // open: Qn, preset, en

  // Other names for the same wires on the sheet: e_PC = e_IR

  // Notes on the sheet:
  //   Data Bus
endmodule
