// Logisim project marie02.circ as structural Verilog: 3 circuits, main circuit main
module main (
  input  start,
  input  reset,
  input  clock,
  output [11:0] out_4,
  output [11:0] out_5,
  output [15:0] out_6,
  output [15:0] out_7,
  output [15:0] out_8,
  output [15:0] out_9
);

  wire demultiplexer_1_out0, demultiplexer_1_out1, demultiplexer_3_out0, demultiplexer_3_out2,
       demultiplexer_3_out3, demultiplexer_3_out4, demultiplexer_3_out5, demultiplexer_3_out6,
       demultiplexer_3_out8, demultiplexer_3_out9, demultiplexer_3_out10, demultiplexer_3_out11,
       demultiplexer_3_out12, demultiplexer_3_out13, demultiplexer_3_out14, demultiplexer_3_out15,
       done_reading, halt, idle_q, l_IR, l_MAR, l_MAR0, l_MAR1, l_MBR, l_PC, mov_inst_to_IR_q, or_1_out,
       or_7_out, or_8_out, or_9_out, or_10_out, or_11_out, \repeat , start_q, start_reading, start_reading0,
       store_data_mbr_q, w_RAM, wait_obtain_data_q, wait_obtain_instruction_q, wait_reading0, wait_reading1;
  wire [11:0] branch_control_next_instruction, multiplexer_1_out;

  D_Flip_Flop idle (.clk(clock), .D(or_1_out), .Q(idle_q), .preset(reset));  // open: Qn, en, reset
  or or_1 (or_1_out, halt, demultiplexer_1_out0);
  Demultiplexer #(.enable("false")) demultiplexer_1 (
    .out0(demultiplexer_1_out0), .out1(demultiplexer_1_out1), .in(idle_q), .sel(start));
  D_Flip_Flop u_start (.clk(clock), .D(demultiplexer_1_out1), .Q(start_q), .reset(reset));  // open: Qn, preset, en
  assign out_9 = 1'b0 ? {4'b0000, out_4} : 16'bz;  // Controlled_Buffer controlled_buffer_1
  assign out_9 = l_MAR0 ? {4'b0000, out_5} : 16'bz;  // Controlled_Buffer controlled_buffer_2
  assign out_9 = l_MAR1 ? out_6 : 16'bz;  // Controlled_Buffer controlled_buffer_3
  assign out_9 = 1'b0 ? out_7 : 16'bz;  // Controlled_Buffer controlled_buffer_4
  assign out_9 = w_RAM ? out_8 : 16'bz;  // Controlled_Buffer controlled_buffer_5
  or or_2 (l_MAR0, start_q, \repeat );
  or or_3 (l_MAR, l_MAR0, l_MAR1);
  or or_4 (start_reading, start_reading0, l_MAR1);
  or or_5 (w_RAM, l_IR, l_MBR);
  or or_6 (l_PC, l_IR, 1'b0);
  branch_control branch_control (.actual_instruction(out_5), .next_instruction(branch_control_next_instruction));
  D_Flip_Flop read_instruction (.clk(clock), .D(l_MAR0), .Q(start_reading0), .reset(reset));  // open: Qn, preset, en
  Register #(.width(12)) MAR (.D(out_9[11:0]), .en(l_MAR), .Q(out_4), .clk(clock), .clr(reset));
  Multiplexer #(.width(12), .enable("false")) multiplexer_1 (
    .in0(out_9[11:0]), .in1(branch_control_next_instruction), .out(multiplexer_1_out), .sel(l_IR));
  Register #(.width(16)) IR (.D(out_9), .en(l_IR), .Q(out_6), .clk(clock), .clr(reset));
  Register #(.width(16)) MBR (.D(out_9), .en(l_MBR), .Q(out_7), .clk(clock), .clr(reset));
  ram_asm ram_asm_1 (
    .address(out_4), .clock(clock), .start(start_reading), .ready(done_reading), .read_data(out_8),
    .data_to_write(out_9));
  Register #(.width(12)) PC (.D(multiplexer_1_out), .en(l_PC), .Q(out_5), .clk(clock), .clr(reset));
  or or_7 (or_7_out, start_reading0, wait_reading0);
  Demultiplexer #(.enable("false")) demultiplexer_2 (
    .out0(wait_reading0), .out1(l_IR), .in(wait_obtain_instruction_q), .sel(done_reading));
  D_Flip_Flop wait_obtain_instruction (
    .clk(clock), .D(or_7_out), .Q(wait_obtain_instruction_q), .reset(reset));  // open: Qn, preset, en
  or or_8 (or_8_out, l_IR, 1'b0);
  D_Flip_Flop mov_inst_to_IR (.clk(clock), .D(or_8_out), .Q(mov_inst_to_IR_q), .reset(reset));  // open: Qn, preset, en
  Demultiplexer #(.select(4), .enable("false")) demultiplexer_3 (
    .out0(demultiplexer_3_out0), .out1(l_MAR1), .out2(demultiplexer_3_out2), .out3(demultiplexer_3_out3),
    .out4(demultiplexer_3_out4), .out5(demultiplexer_3_out5), .out6(demultiplexer_3_out6), .out7(halt),
    .out8(demultiplexer_3_out8), .out9(demultiplexer_3_out9), .out10(demultiplexer_3_out10),
    .out11(demultiplexer_3_out11), .out12(demultiplexer_3_out12), .out13(demultiplexer_3_out13),
    .out14(demultiplexer_3_out14), .out15(demultiplexer_3_out15), .in(mov_inst_to_IR_q), .sel(out_6[15:12]));
  or or_9 (or_9_out, l_MAR1, wait_reading1);
  or or_10 (or_10_out, demultiplexer_3_out0, demultiplexer_3_out2, demultiplexer_3_out3, demultiplexer_3_out4, demultiplexer_3_out5, demultiplexer_3_out6, demultiplexer_3_out8, demultiplexer_3_out9, demultiplexer_3_out10, demultiplexer_3_out11, demultiplexer_3_out12, demultiplexer_3_out13, demultiplexer_3_out14, demultiplexer_3_out15);
  D_Flip_Flop wait_obtain_data (
    .clk(clock), .D(or_9_out), .Q(wait_obtain_data_q), .reset(reset));  // open: Qn, preset, en
  Demultiplexer #(.enable("false")) demultiplexer_4 (
    .out0(wait_reading1), .out1(l_MBR), .in(wait_obtain_data_q), .sel(done_reading));
  or or_11 (or_11_out, l_MBR, 1'b0);
  D_Flip_Flop store_data_mbr (.clk(clock), .D(or_11_out), .Q(store_data_mbr_q), .reset(reset));  // open: Qn, preset, en
  or or_12 (\repeat , store_data_mbr_q, or_10_out);

  // Other names for the same wires on the sheet: IR[15:0] = out_6; ir_write_to_bus[15:0] = out_6; MAR[11:0] = out_4;
  //   mar_write_to_bus[11:0] = out_4; MBR[15:0] = out_7; mbr_write_to_bus[15:0] = out_7; PC[11:0] = out_5;
  //   pc_write_to_bus[11:0] = out_5; ram_write_to_bus[15:0] = out_8; start_reading1 = l_MAR1; w_iR = l_MAR1;
  //   w_iR0 = l_MAR1; w_PC = l_MAR0; w_PC0 = l_MAR0; l_IR0 = l_IR; l_PC0 = l_IR; s_PC = l_IR; s_PC0 = l_IR;
  //   w_RAM0 = l_IR; l_MBR0 = l_MBR; w_RAM1 = l_MBR

  // Notes on the sheet:
  //   Control Unit
  //   Data Bus
  //   Data Bus
  //   Data Bus
  //   Data Bus
  //   Data Bus
  //   Load
endmodule

module ram_asm (
  input  [11:0] address,
  input  clock,
  input  start,
  input  [15:0] data_to_write,
  output ready,
  output [15:0] read_data
);

  Counter #(.width(2), .max('h3)) counter_1 (.carry(ready), .clk(clock), .clr(start));  // open: load, D, count, Q
  RAM #(.addrWidth(12), .dataWidth(16), .bus("separate")) ram_1 (
    .addr(address), .din(data_to_write), .data(read_data), .str(1'b0), .clk(clock), .ld(1'b1));  // open: sel, clr
endmodule

module branch_control (
  input  [11:0] actual_instruction,
  output [11:0] next_instruction
);

  Adder #(.width(12)) adder_1 (.a(actual_instruction), .b(12'h1), .out(next_instruction));  // open: cin, cout
endmodule
