// Logisim project marie03.circ as structural Verilog: 4 circuits, main circuit main
module main (
  input  start,
  input  reset,
  input  clock,
  output [15:0] out_4,
  output [11:0] out_5,
  output [15:0] out_6,
  output [11:0] out_7,
  output [15:0] out_8,
  output [15:0] out_9,
  output [15:0] out_10,
  output [15:0] out_11,
  output [15:0] out_12
);

  wire _000, _400, _800, AC_0, AC_0_t, AC__0, add, and_1_out, and_2_out, and_3_out, clear, d_ff_1_q,
       d_ff_4_q, d_ff_9_q, d_ff_10_q, d_ff_11_q, d_ff_12_q, d_ff_15_q, d_ff_16_q, demultiplexer_1_out0,
       demultiplexer_1_out1, demultiplexer_2_out0, demultiplexer_4_out0, demultiplexer_4_out7,
       demultiplexer_4_out8, demultiplexer_4_out10, demultiplexer_4_out11, demultiplexer_4_out12,
       demultiplexer_4_out13, demultiplexer_4_out14, demultiplexer_4_out15, demultiplexer_5_out0,
       demultiplexer_9_out1, done_operation, enable_keyboard, enable_tty, idle_q, l_AC, l_AC_0, l_AC_1,
       l_AC_3, l_IR, l_MAR, l_MAR0, l_MAR1, l_MAR2, l_MAR3, l_MAR4, l_MBR, l_MBR0, l_MBR1, l_MBR2, l_MBR3,
       l_OUT, l_PC, l_PC1, l_PC2, mov_inst_to_IR_q, no_halt, or_1_out, or_2_out, or_5_out, or_11_out,
       or_15_out, or_18_out, or_19_out, or_20_out, or_21_out, or_22_out, or_23_out, or_24_out, or_25_out,
       or_26_out, \repeat , s_AC, s_PC, skip, start_operation, start_q, start_reading0, start_reading2,
       start_reading3, store_data_mbr_to_ac_q, w_AC, w_iR, w_MBR, w_RAM, wait_obtain_data_2_q,
       wait_obtain_data_3_q, wait_obtain_data_q, wait_obtain_instruction_q, wait_reading0, wait_reading1,
       wait_reading2, wait_reading3, wait_write_data_q, wait_writing0;
  wire [6:0] keyboard_1_data;
  wire [11:0] branch_control_next_instruction, multiplexer_2_out;
  wire [15:0] AC_prime, keyborad_input, multiplexer_1_out;

  Register #(.width(16)) IN (.D(keyborad_input), .en(enable_keyboard), .Q(out_6), .clk(clock), .clr(reset));
  D_Flip_Flop idle (.clk(clock), .D(or_1_out), .Q(idle_q), .preset(reset));  // open: Qn, en, reset
  or or_1 (or_1_out, demultiplexer_2_out0, demultiplexer_1_out0);
  Demultiplexer #(.enable("false")) demultiplexer_1 (
    .out0(demultiplexer_1_out0), .out1(demultiplexer_1_out1), .in(idle_q), .sel(start));
  or or_2 (or_2_out, l_MBR1, start_reading2, start_reading3);
  or or_3 (w_iR, l_MAR1, l_MAR2, l_MAR3, l_MAR4, l_PC1);
  or or_4 (start_operation, start_reading0, l_MAR1, or_2_out);
  alu alu_1 (.AC(out_4), .MBR(out_10), .add(add), .sub(l_AC_3), .clear(clear), .AC_prime(AC_prime));
  assign out_12 = w_AC ? out_4 : 16'bz;  // Controlled_Buffer controlled_buffer_1
  assign out_12 = l_AC_1 ? out_6 : 16'bz;  // Controlled_Buffer controlled_buffer_2
  D_Flip_Flop u_start (.clk(clock), .D(demultiplexer_1_out1), .Q(start_q), .reset(reset));  // open: Qn, preset, en
  Multiplexer #(.width(16), .enable("false")) multiplexer_1 (
    .in0(out_12), .in1(AC_prime), .out(multiplexer_1_out), .sel(s_AC));
  or or_5 (or_5_out, start_q, \repeat );
  Demultiplexer #(.enable("false")) demultiplexer_2 (
    .out0(demultiplexer_2_out0), .out1(l_MAR0), .in(or_5_out), .sel(no_halt));
  or or_6 (l_MBR, l_MBR0, l_MBR1, l_MBR3, l_MBR2);
  or or_7 (s_PC, l_IR, l_PC2);
  or or_8 (s_AC, add, l_AC_3, clear);
  Register #(.width(16)) OUT (.D(out_12), .en(l_OUT), .Q(out_8), .clk(clock), .clr(reset));
  or or_9 (l_MAR, l_MAR0, l_MAR1, l_MAR2, l_MAR3, l_MAR4);
  or or_10 (l_PC, l_IR, l_PC1, l_PC2);
  Register #(.width(16)) AC (.D(multiplexer_1_out), .en(l_AC), .Q(out_4), .clk(clock), .clr(reset));
  D_Flip_Flop read_instruction (.clk(clock), .D(l_MAR0), .Q(start_reading0), .reset(reset));  // open: Qn, preset, en
  TTY #(.rows(4), .cols(7)) tty_1 (.data(out_8[6:0]), .clk(clock), .we(enable_tty), .clr(reset));
  or or_11 (or_11_out, start_reading0, wait_reading0);
  or or_12 (w_AC, l_MBR1, l_OUT);
  D_Flip_Flop wait_obtain_instruction (
    .clk(clock), .D(or_11_out), .Q(wait_obtain_instruction_q), .reset(reset));  // open: Qn, preset, en
  Demultiplexer #(.enable("false")) demultiplexer_3 (
    .out0(wait_reading0), .out1(l_IR), .in(wait_obtain_instruction_q), .sel(done_operation));
  or or_13 (l_AC, l_AC_0, l_AC_1, add, l_AC_3, clear);
  buf or_14 (w_MBR, l_AC_0);  // OR_Gate
  assign out_12 = 1'b0 ? {4'b0000, out_5} : 16'bz;  // Controlled_Buffer controlled_buffer_3
  assign out_12 = l_MAR0 ? {4'b0000, out_7} : 16'bz;  // Controlled_Buffer controlled_buffer_4
  assign out_12 = w_iR ? out_9 : 16'bz;  // Controlled_Buffer controlled_buffer_5
  assign out_12 = w_MBR ? out_10 : 16'bz;  // Controlled_Buffer controlled_buffer_6
  assign out_12 = w_RAM ? out_11 : 16'bz;  // Controlled_Buffer controlled_buffer_7
  Keyboard keyboard_1 (.clk(clock), .re(enable_keyboard), .clr(reset), .data(keyboard_1_data));  // open: avail
  Register #(.width(12)) MAR (.D(out_12[11:0]), .en(l_MAR), .Q(out_5), .clk(clock), .clr(reset));
  branch_control branch_control (.actual_instruction(out_7), .next_instruction(branch_control_next_instruction));
  Register #(.width(16)) IR (.D(out_12), .en(l_IR), .Q(out_9), .clk(clock), .clr(reset));
  Register #(.width(16)) MBR (.D(out_12), .en(l_MBR), .Q(out_10), .clk(clock), .clr(reset));
  or or_15 (or_15_out, l_IR, 1'b0);
  or or_16 (w_RAM, l_IR, l_MBR2, l_MBR0, l_MBR3);
  Multiplexer #(.width(12), .enable("false")) multiplexer_2 (
    .in0(out_12[11:0]), .in1(branch_control_next_instruction), .out(multiplexer_2_out), .sel(s_PC));
  ram_asm ram_asm_1 (
    .address(out_5), .clock(clock), .start(start_operation), .ready(done_operation), .read_data(out_11),
    .data_to_write(out_12), .read_write(l_MBR1));
  Register #(.width(12)) PC (.D(multiplexer_2_out), .en(l_PC), .Q(out_7), .clk(clock), .clr(reset));
  D_Flip_Flop mov_inst_to_IR (.clk(clock), .D(or_15_out), .Q(mov_inst_to_IR_q), .reset(reset));  // open: Qn, preset, en
  assign keyborad_input = {{9{1'b0}}, keyboard_1_data};  // Bit_Extender bit_extender_1
  Comparator #(.width(12), .mode("unsigned")) comparator_1 (
    .a(out_9[11:0]), .b({12{1'b0}}), .eq(_000));  // open: gt, lt
  Comparator #(.width(12), .mode("unsigned")) comparator_2 (.a(out_9[11:0]), .b(12'h400), .eq(_400));  // open: gt, lt
  Comparator #(.width(12), .mode("unsigned")) comparator_3 (.a(out_9[11:0]), .b(12'h800), .eq(_800));  // open: gt, lt
  and and_1 (and_1_out, _400, AC__0);
  Comparator #(.width(16)) comparator_4 (.a(out_4), .b({16{1'b0}}), .gt(AC_0_t), .eq(AC__0), .lt(AC_0));
  and and_2 (and_2_out, _000, AC_0);
  and and_3 (and_3_out, AC_0_t, _800);
  Demultiplexer #(.select(4), .enable("false")) demultiplexer_4 (
    .out0(demultiplexer_4_out0), .out1(l_MAR1), .out2(l_MAR2), .out3(l_MAR3), .out4(l_MAR4),
    .out5(enable_keyboard), .out6(l_OUT), .out7(demultiplexer_4_out7), .out8(demultiplexer_4_out8),
    .out9(l_PC1), .out10(demultiplexer_4_out10), .out11(demultiplexer_4_out11),
    .out12(demultiplexer_4_out12), .out13(demultiplexer_4_out13), .out14(demultiplexer_4_out14),
    .out15(demultiplexer_4_out15), .in(mov_inst_to_IR_q), .sel(out_9[15:12]));
  or or_17 (skip, and_2_out, and_1_out, and_3_out);
  or or_18 (or_18_out, l_MAR2, 1'b0);
  not not_1 (no_halt, demultiplexer_4_out7);
  Demultiplexer #(.enable("false")) demultiplexer_5 (
    .out0(demultiplexer_5_out0), .out1(l_PC2), .in(d_ff_1_q), .sel(skip));
  D_Flip_Flop d_ff_1 (.clk(clock), .D(demultiplexer_4_out8), .Q(d_ff_1_q), .reset(reset));  // open: Qn, preset, en
  or or_19 (or_19_out, l_MAR1, wait_reading1);
  D_Flip_Flop d_ff_2 (.clk(clock), .D(or_18_out), .Q(l_MBR1), .reset(reset));  // open: Qn, preset, en
  or or_20 (or_20_out, l_MAR3, 1'b0);
  or or_21 (or_21_out, l_MAR4, 1'b0);
  D_Flip_Flop d_ff_3 (.clk(clock), .D(l_OUT), .Q(enable_tty), .reset(reset));  // open: Qn, preset, en
  D_Flip_Flop d_ff_4 (.clk(clock), .D(l_PC1), .Q(d_ff_4_q), .reset(reset));  // open: Qn, preset, en
  D_Flip_Flop d_ff_5 (.clk(clock), .D(demultiplexer_4_out10), .Q(clear), .reset(reset));  // open: Qn, preset, en
  D_Flip_Flop wait_obtain_data (
    .clk(clock), .D(or_19_out), .Q(wait_obtain_data_q), .reset(reset));  // open: Qn, preset, en
  Demultiplexer #(.enable("false")) demultiplexer_6 (
    .out0(wait_reading1), .out1(l_MBR0), .in(wait_obtain_data_q), .sel(done_operation));
  D_Flip_Flop d_ff_6 (.clk(clock), .D(or_20_out), .Q(start_reading2), .reset(reset));  // open: Qn, preset, en
  D_Flip_Flop d_ff_7 (.clk(clock), .D(or_21_out), .Q(start_reading3), .reset(reset));  // open: Qn, preset, en
  D_Flip_Flop d_ff_8 (.clk(clock), .D(enable_keyboard), .Q(l_AC_1), .reset(reset));  // open: Qn, preset, en
  or or_22 (or_22_out, start_reading2, wait_reading2);
  or or_23 (or_23_out, start_reading3, wait_reading3);
  D_Flip_Flop d_ff_9 (.clk(clock), .D(enable_tty), .Q(d_ff_9_q), .reset(reset));  // open: Qn, preset, en
  or or_24 (or_24_out, demultiplexer_5_out0, l_PC2);
  D_Flip_Flop d_ff_10 (.clk(clock), .D(clear), .Q(d_ff_10_q), .reset(reset));  // open: Qn, preset, en
  D_Flip_Flop wait_obtain_data_2 (
    .clk(clock), .D(or_22_out), .Q(wait_obtain_data_2_q), .reset(reset));  // open: Qn, preset, en
  D_Flip_Flop wait_obtain_data_3 (
    .clk(clock), .D(or_23_out), .Q(wait_obtain_data_3_q), .reset(reset));  // open: Qn, preset, en
  D_Flip_Flop d_ff_11 (.clk(clock), .D(l_AC_1), .Q(d_ff_11_q), .reset(reset));  // open: Qn, preset, en
  D_Flip_Flop d_ff_12 (.clk(clock), .D(or_24_out), .Q(d_ff_12_q), .reset(reset));  // open: Qn, preset, en
  or or_25 (or_25_out, l_MBR0, 1'b0);
  or or_26 (or_26_out, l_MBR1, wait_writing0);
  Demultiplexer #(.enable("false")) demultiplexer_7 (
    .out0(wait_reading2), .out1(l_MBR2), .in(wait_obtain_data_2_q), .sel(done_operation));
  Demultiplexer #(.enable("false")) demultiplexer_8 (
    .out0(wait_reading3), .out1(l_MBR3), .in(wait_obtain_data_3_q), .sel(done_operation));
  D_Flip_Flop wait_write_data (
    .clk(clock), .D(or_26_out), .Q(wait_write_data_q), .reset(reset));  // open: Qn, preset, en
  Demultiplexer #(.enable("false")) demultiplexer_9 (
    .out0(wait_writing0), .out1(demultiplexer_9_out1), .in(wait_write_data_q), .sel(done_operation));
  D_Flip_Flop store_data_mbr (.clk(clock), .D(or_25_out), .Q(l_AC_0), .reset(reset));  // open: Qn, preset, en
  D_Flip_Flop d_ff_13 (.clk(clock), .D(l_MBR3), .Q(l_AC_3), .reset(reset));  // open: Qn, preset, en
  D_Flip_Flop d_ff_14 (.clk(clock), .D(l_MBR2), .Q(add), .reset(reset));  // open: Qn, preset, en
  D_Flip_Flop store_data_mbr_to_ac (
    .clk(clock), .D(l_AC_0), .Q(store_data_mbr_to_ac_q), .reset(reset));  // open: Qn, preset, en
  D_Flip_Flop d_ff_15 (.clk(clock), .D(add), .Q(d_ff_15_q), .reset(reset));  // open: Qn, preset, en
  D_Flip_Flop d_ff_16 (.clk(clock), .D(l_AC_3), .Q(d_ff_16_q), .reset(reset));  // open: Qn, preset, en
  or or_27 (\repeat , store_data_mbr_to_ac_q, demultiplexer_9_out1, d_ff_15_q, d_ff_16_q, d_ff_11_q, d_ff_9_q, demultiplexer_4_out7, d_ff_12_q, d_ff_4_q, d_ff_10_q);

  // Other names for the same wires on the sheet: AC[15:0] = out_4; ac_write_to_bus[15:0] = out_4; IN[15:0] = out_6;
  //   IR[15:0] = out_9; ir_write_to_bus[15:0] = out_9; l_IN = enable_keyboard; MAR[11:0] = out_5;
  //   mar_write_to_bus[11:0] = out_5; MBR[15:0] = out_10; mbr_write_to_bus[15:0] = out_10; PC[11:0] = out_7;
  //   pc_write_to_bus[11:0] = out_7; ram_write_to_bus[15:0] = out_11; l_AC_2 = add; s_AC0 = add; l_AC_4 = clear;
  //   s_AC2 = clear; s_PC1 = l_PC2; s_AC1 = l_AC_3; sub = l_AC_3; w_AC1 = l_OUT; w_IN = l_AC_1;
  //   start_reading1 = l_MAR1; w_iR0 = l_MAR1; w_iR1 = l_MAR2; w_iR2 = l_MAR3; w_iR3 = l_MAR4; w_iR4 = l_PC1;
  //   w_MBR_0 = l_AC_0; w_PC = l_MAR0; w_PC0 = l_MAR0; l_IR0 = l_IR; l_PC0 = l_IR; s_PC0 = l_IR; w_RAM0 = l_IR;
  //   w_RAM1 = l_MBR0; w_RAM2 = l_MBR2; w_RAM3 = l_MBR3; start_writing0 = l_MBR1; w_AC0 = l_MBR1;
  //   write_enable = l_MBR1; write_enable0 = l_MBR1

  // Notes on the sheet:
  //   Control Unit
  //   Data Bus
  //   Data Bus
  //   Data Bus
  //   Data Bus
  //   Data Bus
  //   Data Bus
  //   Data Bus
  //   Jns
  //   Load
  //   Store
  //   Add
  //   Subt
  //   Input
  //   Output
  //   SkipCond
  //   Jump
  //   Clear
endmodule

module ram_asm (
  input  [11:0] address,
  input  clock,
  input  start,
  input  read_write,
  input  [15:0] data_to_write,
  output ready,
  output [15:0] read_data
);

  wire not_1_out;

  RAM #(.addrWidth(12), .dataWidth(16), .bus("separate")) ram_1 (
    .addr(address), .din(data_to_write), .data(read_data), .str(read_write), .clk(clock), .ld(not_1_out));  // open: sel, clr
  not not_1 (not_1_out, read_write);
  Counter #(.width(1), .max('h1)) counter_1 (.carry(ready), .clk(clock), .clr(start));  // open: load, D, count, Q
endmodule

module branch_control (
  input  [11:0] actual_instruction,
  output [11:0] next_instruction
);

  Adder #(.width(12)) adder_1 (.a(actual_instruction), .b(12'h1), .out(next_instruction));  // open: cin, cout
endmodule

module alu (
  input  [15:0] AC,
  input  [15:0] MBR,
  input  add,
  input  sub,
  input  clear,
  output [15:0] AC_prime
);

  wire [15:0] adder_1_out, subtractor_1_out;

  Adder #(.width(16)) adder_1 (.a(AC), .b(MBR), .out(adder_1_out));  // open: cin, cout
  Subtractor #(.width(16)) subtractor_1 (.a(AC), .b(MBR), .out(subtractor_1_out));  // open: bin, bout
  Multiplexer #(.select(3), .width(16), .enable("false")) multiplexer_1 (
    .in0({16{1'b0}}), .in1(adder_1_out), .in2(subtractor_1_out), .in3({16{1'b0}}), .in4({16{1'b0}}),
    .in5({16{1'b0}}), .in6({16{1'b0}}), .in7({16{1'b0}}), .out(AC_prime), .sel({clear, sub, add}));
endmodule
