// Logisim project marie04.circ as structural Verilog: 5 circuits, main circuit main
module main (
  input  start,
  input  reset,
  output [15:0] out_3,
  output [11:0] out_4,
  output [15:0] out_5,
  output [11:0] out_6,
  output [15:0] out_7,
  output [15:0] out_8,
  output [15:0] out_9,
  output [15:0] out_10,
  output [15:0] out_11
);

  wire _000, _400, _800, AC_0, AC_0_t, AC__0, add, add1, add2, and_1_out, and_2_out, and_3_out, clear, clock,
       controlled_buffer_8_out, d_ff_5_q, d_ff_11_q, d_ff_12_q, d_ff_14_q, d_ff_15_q, d_ff_16_q, d_ff_19_q,
       d_ff_20_q, d_ff_21_q, d_ff_22_q, d_ff_24_q, d_ff_25_q, demultiplexer_1_out0, demultiplexer_1_out1,
       demultiplexer_2_out0, demultiplexer_4_out7, demultiplexer_4_out8, demultiplexer_4_out10,
       demultiplexer_4_out11, demultiplexer_4_out12, demultiplexer_4_out13, demultiplexer_4_out14,
       demultiplexer_4_out15, demultiplexer_5_out0, demultiplexer_5_out1, demultiplexer_8_out1,
       demultiplexer_13_out1, done_operation, emp, enable_keyboard, enable_tty, fstate, idle_q, is_addl,
       is_jumpl, is_store, l_AC, l_AC_0, l_AC_1, l_AC_3, l_AC_11, l_IR, l_MAR, l_MAR0, l_MAR1, l_MAR2,
       l_MAR3, l_MAR4, l_MAR5, l_MAR9, l_MBR, l_MBR0, l_MBR1, l_MBR2, l_MBR3, l_MBR4, l_MBR7, l_MBR8, l_OUT,
       l_PC, l_PC1, l_PC2, l_PC5, l_PC6, mov_inst_to_IR_q, no_halt, or_1_out, or_2_out, or_3_out, or_7_out,
       or_8_out, or_9_out, or_10_out, or_12_out, or_16_out, or_19_out, or_20_out, or_22_out, or_23_out,
       or_28_out, or_30_out, or_32_out, or_33_out, or_34_out, or_35_out, or_36_out, or_38_out, or_39_out,
       or_40_out, or_41_out, or_42_out, or_43_out, or_44_out, or_45_out, or_46_out, \repeat , s_AC, s_PC,
       skip, start_operation, start_q, start_reading0, start_reading2, start_reading3, start_reading5,
       start_reading6, start_writing1, start_writing4, store_data_mbr_to_ac_q, w_AC, w_iR, w_MAR, w_MBR,
       w_PC, w_RAM, wait_obtain_data_2_q, wait_obtain_data_3_q, wait_obtain_data_4_q, wait_obtain_data_5_q,
       wait_obtain_data_q, wait_obtain_instruction_q, wait_reading0, wait_reading1, wait_reading2,
       wait_reading3, wait_reading5, wait_reading6, wait_write_data_2_q, wait_write_data_3_q,
       wait_write_data_q, wait_writing0, wait_writing1, wait_writing6, write_enable;
  wire [2:0] counter_1_q;
  wire [11:0] branch_control_next_instruction, multiplexer_2_out;
  wire [15:0] AC_prime, keyborad_input, multiplexer_1_out;

  Register #(.width(16)) IN (.D(keyborad_input), .en(enable_keyboard), .Q(out_5), .clk(clock), .clr(reset));
  D_Flip_Flop idle (.clk(clock), .D(or_2_out), .Q(idle_q), .preset(reset));  // open: Qn, en, reset
  or or_1 (or_1_out, l_MAR9, l_PC1, l_MAR5);
  or or_2 (or_2_out, demultiplexer_2_out0, demultiplexer_1_out0);
  Demultiplexer #(.enable("false")) demultiplexer_1 (
    .out0(demultiplexer_1_out0), .out1(demultiplexer_1_out1), .in(idle_q), .sel(start));
  or or_3 (or_3_out, start_reading6, start_writing4, start_reading5);
  or or_4 (write_enable, l_MBR1, start_writing4, start_writing1);
  or or_5 (w_iR, l_MAR1, l_MAR2, l_MAR3, l_MAR4, or_1_out);
  or or_6 (start_operation, start_reading0, l_MAR1, or_7_out);
  or or_7 (or_7_out, l_MBR1, start_reading2, start_reading3, start_writing1, or_3_out);
  alu alu_1 (.AC(out_3), .MBR(out_9), .add(add), .sub(l_AC_3), .clear(clear), .AC_prime(AC_prime));
  assign out_11 = w_AC ? out_3 : 16'bz;  // Controlled_Buffer controlled_buffer_1
  assign out_11 = l_AC_1 ? out_5 : 16'bz;  // Controlled_Buffer controlled_buffer_2
  D_Flip_Flop u_start (.clk(clock), .D(demultiplexer_1_out1), .Q(start_q), .reset(reset));  // open: Qn, preset, en
  or or_8 (or_8_out, l_MBR8, l_MBR7, l_MBR4);
  or or_9 (or_9_out, l_PC2, fstate, l_PC6, l_PC5);
  Multiplexer #(.width(16), .enable("false")) multiplexer_1 (
    .in0(out_11), .in1(AC_prime), .out(multiplexer_1_out), .sel(s_AC));
  Demultiplexer #(.enable("false")) demultiplexer_2 (
    .out0(demultiplexer_2_out0), .out1(l_MAR0), .in(or_10_out), .sel(no_halt));
  or or_10 (or_10_out, start_q, \repeat );
  or or_11 (l_MBR, l_MBR0, l_MBR1, l_MBR3, l_MBR2, or_8_out);
  or or_12 (or_12_out, clear, add2);
  or or_13 (l_PC, l_IR, l_PC1, or_9_out);
  Register #(.width(16)) OUT (.D(out_11), .en(l_OUT), .Q(out_7), .clk(clock), .clr(reset));
  or or_14 (w_PC, l_MAR0, l_MBR4);
  or or_15 (s_PC, l_IR, or_16_out);
  or or_16 (or_16_out, l_PC2, l_PC6);
  or or_17 (s_AC, add1, l_AC_3, or_12_out);
  Register #(.width(16)) AC (.D(multiplexer_1_out), .en(l_AC), .Q(out_3), .clk(clock), .clr(reset));
  D_Flip_Flop read_instruction (.clk(clock), .D(l_MAR0), .Q(start_reading0), .reset(reset));  // open: Qn, preset, en
  or or_18 (l_MAR, l_MAR0, l_MAR1, l_MAR2, l_MAR3, or_19_out);
  or or_19 (or_19_out, l_MAR5, emp, l_MAR9, l_MAR4);
  TTY #(.rows(4), .cols(20)) tty_1 (.data(out_7[6:0]), .clk(clock), .we(enable_tty), .clr(reset));
  or or_20 (or_20_out, l_AC_11, emp, fstate);
  or or_21 (add, add1, add2);
  or or_22 (or_22_out, start_reading0, wait_reading0);
  or or_23 (or_23_out, add2, clear, l_AC_11);
  D_Flip_Flop wait_obtain_instruction (
    .clk(clock), .D(or_22_out), .Q(wait_obtain_instruction_q), .reset(reset));  // open: Qn, preset, en
  Demultiplexer #(.enable("false")) demultiplexer_3 (
    .out0(wait_reading0), .out1(l_IR), .in(wait_obtain_instruction_q), .sel(done_operation));
  buf or_24 (w_MAR, l_PC5);  // OR_Gate
  or or_25 (w_AC, l_MBR1, l_OUT, start_writing4);
  or or_26 (l_AC, l_AC_0, l_AC_1, add1, l_AC_3, or_23_out);
  or or_27 (w_MBR, l_AC_0, or_20_out, start_writing1);
  assign out_11 = w_MAR ? {4'b0000, out_4} : 16'bz;  // Controlled_Buffer controlled_buffer_3
  assign out_11 = w_PC ? {4'b0000, out_6} : 16'bz;  // Controlled_Buffer controlled_buffer_4
  assign out_11 = w_iR ? out_8 : 16'bz;  // Controlled_Buffer controlled_buffer_5
  assign out_11 = w_MBR ? out_9 : 16'bz;  // Controlled_Buffer controlled_buffer_6
  assign out_11 = w_RAM ? out_10 : 16'bz;  // Controlled_Buffer controlled_buffer_7
  assign controlled_buffer_8_out = enable_keyboard ? clock : 1'bz;  // Controlled_Buffer controlled_buffer_8
  Comparator #(.width(16)) comparator_1 (.a(out_3), .b({16{1'b0}}), .gt(AC_0_t), .eq(AC__0), .lt(AC_0));
  Counter #(.width(3), .max('h7)) counter_1 (
    .Q(counter_1_q), .clk(controlled_buffer_8_out), .clr(reset));  // open: load, D, count, carry
  Register #(.width(12)) MAR (.D(out_11[11:0]), .en(l_MAR), .Q(out_4), .clk(clock), .clr(reset));
  branch_control branch_control (.actual_instruction(out_6), .next_instruction(branch_control_next_instruction));
  Register #(.width(16)) IR (.D(out_11), .en(l_IR), .Q(out_8), .clk(clock), .clr(reset));
  Register #(.width(16)) MBR (.D(out_11), .en(l_MBR), .Q(out_9), .clk(clock), .clr(reset));
  or or_28 (or_28_out, l_IR, 1'b0);
  or or_29 (w_RAM, l_IR, l_MBR2, l_MBR0, or_30_out);
  or or_30 (or_30_out, l_MBR3, l_MBR8, l_MBR7);
  Multiplexer #(.width(12), .enable("false")) multiplexer_2 (
    .in0(out_11[11:0]), .in1(branch_control_next_instruction), .out(multiplexer_2_out), .sel(s_PC));
  ram_asm ram_asm_1 (
    .address(out_4), .clock(clock), .start(start_operation), .ready(done_operation), .read_data(out_10),
    .data_to_write(out_11), .read_write(write_enable));
  instruction_decoder Instruction_Decoder (
    .IR(out_8), .addi(is_addl), .jumpi(is_jumpl), .storei(is_store), ._000(_000), ._400(_400), ._800(_800));  // open: loadi
  and and_1 (and_1_out, _400, AC__0);
  Register #(.width(12)) PC (.D(multiplexer_2_out), .en(l_PC), .Q(out_6), .clk(clock), .clr(reset));
  D_Flip_Flop mov_inst_to_IR (.clk(clock), .D(or_28_out), .Q(mov_inst_to_IR_q), .reset(reset));  // open: Qn, preset, en
  ROM #(.addrWidth(3), .dataWidth(16)) rom_1 (.addr(counter_1_q), .data(keyborad_input));  // open: sel
  and and_2 (and_2_out, _000, AC_0);
  and and_3 (and_3_out, AC_0_t, _800);
  or or_31 (skip, and_2_out, and_1_out, and_3_out);
  Clock clock_1 (.out(clock));
  Demultiplexer #(.select(4), .enable("false")) demultiplexer_4 (
    .out0(l_MAR5), .out1(l_MAR1), .out2(l_MAR2), .out3(l_MAR3), .out4(l_MAR4), .out5(enable_keyboard),
    .out6(l_OUT), .out7(demultiplexer_4_out7), .out8(demultiplexer_4_out8), .out9(l_PC1),
    .out10(demultiplexer_4_out10), .out11(demultiplexer_4_out11), .out12(demultiplexer_4_out12),
    .out13(demultiplexer_4_out13), .out14(demultiplexer_4_out14), .out15(demultiplexer_4_out15),
    .in(mov_inst_to_IR_q), .sel(out_8[15:12]));
  Demultiplexer #(.enable("false")) demultiplexer_5 (
    .out0(demultiplexer_5_out0), .out1(demultiplexer_5_out1), .in(demultiplexer_4_out8), .sel(skip));
  or or_32 (or_32_out, start_reading6, wait_reading6);
  D_Flip_Flop d_ff_1 (.clk(clock), .D(l_MAR5), .Q(l_MBR4), .reset(reset));  // open: Qn, preset, en
  or or_33 (or_33_out, l_MAR2, 1'b0);
  not not_1 (no_halt, demultiplexer_4_out7);
  D_Flip_Flop d_ff_2 (.clk(clock), .D(demultiplexer_5_out1), .Q(l_PC2), .reset(reset));  // open: Qn, preset, en
  D_Flip_Flop wait_obtain_data (
    .clk(clock), .D(or_32_out), .Q(wait_obtain_data_q), .reset(reset));  // open: Qn, preset, en
  or or_34 (or_34_out, l_MAR1, wait_reading1);
  D_Flip_Flop d_ff_3 (.clk(clock), .D(or_33_out), .Q(l_MBR1), .reset(reset));  // open: Qn, preset, en
  or or_35 (or_35_out, l_MAR3, 1'b0);
  or or_36 (or_36_out, l_MAR4, 1'b0);
  D_Flip_Flop d_ff_4 (.clk(clock), .D(l_OUT), .Q(enable_tty), .reset(reset));  // open: Qn, preset, en
  D_Flip_Flop d_ff_5 (.clk(clock), .D(l_PC1), .Q(d_ff_5_q), .reset(reset));  // open: Qn, preset, en
  D_Flip_Flop d_ff_6 (.clk(clock), .D(demultiplexer_4_out10), .Q(clear), .reset(reset));  // open: Qn, preset, en
  or or_37 (l_MAR9, demultiplexer_4_out11, demultiplexer_4_out12, demultiplexer_4_out13, demultiplexer_4_out14);
  Demultiplexer #(.enable("false")) demultiplexer_6 (
    .out0(wait_reading6), .out1(l_MBR8), .in(wait_obtain_data_q), .sel(done_operation));
  or or_38 (or_38_out, start_writing4, wait_writing6);
  D_Flip_Flop wait_obtain_data_2 (
    .clk(clock), .D(or_34_out), .Q(wait_obtain_data_2_q), .reset(reset));  // open: Qn, preset, en
  Demultiplexer #(.enable("false")) demultiplexer_7 (
    .out0(wait_reading1), .out1(l_MBR0), .in(wait_obtain_data_2_q), .sel(done_operation));
  D_Flip_Flop d_ff_7 (.clk(clock), .D(or_35_out), .Q(start_reading2), .reset(reset));  // open: Qn, preset, en
  D_Flip_Flop d_ff_8 (.clk(clock), .D(or_36_out), .Q(start_reading3), .reset(reset));  // open: Qn, preset, en
  D_Flip_Flop d_ff_9 (.clk(clock), .D(enable_keyboard), .Q(l_AC_1), .reset(reset));  // open: Qn, preset, en
  D_Flip_Flop d_ff_10 (.clk(clock), .D(l_MAR9), .Q(start_reading5), .reset(reset));  // open: Qn, preset, en
  or or_39 (or_39_out, start_reading2, wait_reading2);
  or or_40 (or_40_out, start_reading3, wait_reading3);
  D_Flip_Flop d_ff_11 (.clk(clock), .D(enable_tty), .Q(d_ff_11_q), .reset(reset));  // open: Qn, preset, en
  or or_41 (or_41_out, demultiplexer_5_out0, l_PC2);
  D_Flip_Flop d_ff_12 (.clk(clock), .D(clear), .Q(d_ff_12_q), .reset(reset));  // open: Qn, preset, en
  Demultiplexer #(.enable("false")) demultiplexer_8 (
    .out0(wait_writing6), .out1(demultiplexer_8_out1), .in(wait_write_data_q), .sel(done_operation));
  D_Flip_Flop wait_write_data (
    .clk(clock), .D(or_38_out), .Q(wait_write_data_q), .reset(reset));  // open: Qn, preset, en
  D_Flip_Flop d_ff_13 (.clk(clock), .D(l_MBR4), .Q(start_writing1), .reset(reset));  // open: Qn, preset, en
  D_Flip_Flop wait_obtain_data_3 (
    .clk(clock), .D(or_39_out), .Q(wait_obtain_data_3_q), .reset(reset));  // open: Qn, preset, en
  D_Flip_Flop wait_obtain_data_4 (
    .clk(clock), .D(or_40_out), .Q(wait_obtain_data_4_q), .reset(reset));  // open: Qn, preset, en
  D_Flip_Flop d_ff_14 (.clk(clock), .D(l_AC_1), .Q(d_ff_14_q), .reset(reset));  // open: Qn, preset, en
  D_Flip_Flop d_ff_15 (.clk(clock), .D(or_41_out), .Q(d_ff_15_q), .reset(reset));  // open: Qn, preset, en
  or or_42 (or_42_out, start_reading5, wait_reading5);
  Demultiplexer #(.enable("false")) demultiplexer_9 (.out0(l_AC_11), .out1(add2), .in(d_ff_16_q), .sel(is_addl));
  D_Flip_Flop d_ff_16 (.clk(clock), .D(l_MBR8), .Q(d_ff_16_q), .reset(reset));  // open: Qn, preset, en
  or or_43 (or_43_out, l_MBR0, 1'b0);
  or or_44 (or_44_out, l_MBR1, wait_writing0);
  Demultiplexer #(.enable("false")) demultiplexer_10 (
    .out0(wait_reading2), .out1(l_MBR2), .in(wait_obtain_data_3_q), .sel(done_operation));
  Demultiplexer #(.enable("false")) demultiplexer_11 (
    .out0(wait_reading3), .out1(l_MBR3), .in(wait_obtain_data_4_q), .sel(done_operation));
  D_Flip_Flop wait_obtain_data_5 (
    .clk(clock), .D(or_42_out), .Q(wait_obtain_data_5_q), .reset(reset));  // open: Qn, preset, en
  Demultiplexer #(.enable("false")) demultiplexer_12 (
    .out0(wait_reading5), .out1(l_MBR7), .in(wait_obtain_data_5_q), .sel(done_operation));
  D_Flip_Flop wait_write_data_2 (
    .clk(clock), .D(or_44_out), .Q(wait_write_data_2_q), .reset(reset));  // open: Qn, preset, en
  Demultiplexer #(.enable("false")) demultiplexer_13 (
    .out0(wait_writing0), .out1(demultiplexer_13_out1), .in(wait_write_data_2_q), .sel(done_operation));
  or or_45 (or_45_out, start_writing1, wait_writing1);
  D_Flip_Flop store_data_mbr (.clk(clock), .D(or_43_out), .Q(l_AC_0), .reset(reset));  // open: Qn, preset, en
  D_Flip_Flop d_ff_17 (.clk(clock), .D(l_MBR3), .Q(l_AC_3), .reset(reset));  // open: Qn, preset, en
  Demultiplexer #(.enable("false")) demultiplexer_14 (.out0(emp), .out1(fstate), .in(d_ff_19_q), .sel(is_jumpl));
  Demultiplexer #(.enable("false")) demultiplexer_15 (
    .out0(wait_writing1), .out1(l_PC5), .in(wait_write_data_3_q), .sel(done_operation));
  D_Flip_Flop wait_write_data_3 (
    .clk(clock), .D(or_45_out), .Q(wait_write_data_3_q), .reset(reset));  // open: Qn, preset, en
  D_Flip_Flop d_ff_18 (.clk(clock), .D(l_MBR2), .Q(add1), .reset(reset));  // open: Qn, preset, en
  D_Flip_Flop d_ff_19 (.clk(clock), .D(l_MBR7), .Q(d_ff_19_q), .reset(reset));  // open: Qn, preset, en
  D_Flip_Flop store_data_mbr_to_ac (
    .clk(clock), .D(l_AC_0), .Q(store_data_mbr_to_ac_q), .reset(reset));  // open: Qn, preset, en
  or or_46 (or_46_out, l_AC_11, add2, demultiplexer_8_out1, fstate);
  D_Flip_Flop d_ff_20 (.clk(clock), .D(l_AC_3), .Q(d_ff_20_q), .reset(reset));  // open: Qn, preset, en
  D_Flip_Flop d_ff_21 (.clk(clock), .D(emp), .Q(d_ff_21_q), .reset(reset));  // open: Qn, preset, en
  Demultiplexer #(.enable("false")) demultiplexer_16 (
    .out0(start_reading6), .out1(start_writing4), .in(d_ff_21_q), .sel(is_store));
  D_Flip_Flop d_ff_22 (.clk(clock), .D(or_46_out), .Q(d_ff_22_q), .reset(reset));  // open: Qn, preset, en
  D_Flip_Flop d_ff_23 (.clk(clock), .D(l_PC5), .Q(l_PC6), .reset(reset));  // open: Qn, preset, en
  D_Flip_Flop d_ff_24 (.clk(clock), .D(add1), .Q(d_ff_24_q), .reset(reset));  // open: Qn, preset, en
  D_Flip_Flop d_ff_25 (.clk(clock), .D(l_PC6), .Q(d_ff_25_q), .reset(reset));  // open: Qn, preset, en
  or or_47 (\repeat , d_ff_25_q, store_data_mbr_to_ac_q, demultiplexer_13_out1, d_ff_24_q, d_ff_20_q, d_ff_14_q, d_ff_11_q, demultiplexer_4_out7, d_ff_15_q, d_ff_5_q, d_ff_12_q, d_ff_22_q);

  // Other names for the same wires on the sheet: AC[15:0] = out_3; ac_write_to_bus[15:0] = out_3; IN[15:0] = out_5;
  //   IR[15:0] = out_8; ir_write_to_bus[15:0] = out_8; l_IN = enable_keyboard; MAR[11:0] = out_4;
  //   mar_write_to_bus[11:0] = out_4; MBR[15:0] = out_9; mbr_write_to_bus[15:0] = out_9; PC[11:0] = out_6;
  //   pc_write_to_bus[11:0] = out_6; ram_write_to_bus[15:0] = out_10; l_AC_2 = add1; s_AC0 = add1; l_AC_4 = clear;
  //   s_AC2 = clear; l_AC_12 = add2; s_AC3 = add2; s_PC1 = l_PC2; s_PC4 = l_PC6; s_AC1 = l_AC_3; sub = l_AC_3;
  //   w_AC1 = l_OUT; w_IN = l_AC_1; start_reading1 = l_MAR1; w_iR0 = l_MAR1; w_iR1 = l_MAR2; w_iR2 = l_MAR3;
  //   w_iR3 = l_MAR4; w_iR4 = l_PC1; w_iR5 = l_MAR5; w_iR9 = l_MAR9; w_MAR0 = l_PC5; l_MAR10 = emp; w_MBR6 = emp;
  //   w_MBR11 = l_AC_11; l_PC12 = fstate; w_MBR12 = fstate; w_MBR_0 = l_AC_0; w_PC0 = l_MAR0; w_PC1 = l_MBR4;
  //   l_IR0 = l_IR; l_PC0 = l_IR; s_PC0 = l_IR; w_RAM0 = l_IR; w_RAM1 = l_MBR0; w_RAM2 = l_MBR2; w_RAM3 = l_MBR3;
  //   w_RAM7 = l_MBR7; w_RAM8 = l_MBR8; start_writing0 = l_MBR1; w_AC0 = l_MBR1; write_enable0 = l_MBR1;
  //   w_MBR5 = start_writing1; write_enable1 = start_writing1; storel_work = start_writing4; w_AC11 = start_writing4;
  //   write_enable5 = start_writing4

  // Notes on the sheet:
  //   Control Unit
  //   Data Bus
  //   Data Bus
  //   Data Bus
  //   Data Bus
  //   Data Bus
  //   Data Bus
  //   Data Bus
  //   contents of rom_1 (hex, n*v repeats v):
  //   7 2a 29 28 27 26 25 24
  //   Loadl
  //   Jns
  //   Load
  //   Store
  //   Add
  //   Subt
  //   Input
  //   Output
  //   Jump
  //   Clear
  //   Addl
  //   Jumpl
  //   Storel
  //   Loadl
  //   Storel
  //   SkipCond
endmodule

module ram_asm (
  input  [11:0] address,
  input  clock,
  input  start,
  input  read_write,
  input  [15:0] data_to_write,
  output ready,
  output [15:0] read_data
);

  wire not_1_out;

  RAM #(.addrWidth(12), .dataWidth(16), .bus("separate")) ram_1 (
    .addr(address), .din(data_to_write), .data(read_data), .str(read_write), .clk(clock), .ld(not_1_out));  // open: sel, clr
  not not_1 (not_1_out, read_write);
  Counter #(.width(1), .max('h1)) counter_1 (.carry(ready), .clk(clock), .clr(start));  // open: load, D, count, Q
endmodule

module branch_control (
  input  [11:0] actual_instruction,
  output [11:0] next_instruction
);

  Adder #(.width(12)) adder_1 (.a(actual_instruction), .b(12'h1), .out(next_instruction));  // open: cin, cout
endmodule

module alu (
  input  [15:0] AC,
  input  [15:0] MBR,
  input  add,
  input  sub,
  input  clear,
  output [15:0] AC_prime
);

  wire [15:0] adder_1_out, subtractor_1_out;

  Adder #(.width(16)) adder_1 (.a(AC), .b(MBR), .out(adder_1_out));  // open: cin, cout
  Subtractor #(.width(16)) subtractor_1 (.a(AC), .b(MBR), .out(subtractor_1_out));  // open: bin, bout
  Multiplexer #(.select(3), .width(16), .enable("false")) multiplexer_1 (
    .in0({16{1'b0}}), .in1(adder_1_out), .in2(subtractor_1_out), .in3({16{1'b0}}), .in4({16{1'b0}}),
    .in5({16{1'b0}}), .in6({16{1'b0}}), .in7({16{1'b0}}), .out(AC_prime), .sel({clear, sub, add}));
endmodule

module instruction_decoder (
  input  [15:0] IR,
  output addi,
  output jumpi,
  output loadi,
  output storei,
  output _000,
  output _400,
  output _800
);

  Comparator #(.width(4), .mode("unsigned")) comparator_1 (.a(IR[15:12]), .b(4'b1011), .eq(addi));  // open: gt, lt
  Comparator #(.width(4), .mode("unsigned")) comparator_2 (.a(IR[15:12]), .b(4'b1100), .eq(jumpi));  // open: gt, lt
  Comparator #(.width(4), .mode("unsigned")) comparator_3 (.a(IR[15:12]), .b(4'b1101), .eq(loadi));  // open: gt, lt
  Comparator #(.width(4), .mode("unsigned")) comparator_4 (.a(IR[15:12]), .b(4'b1110), .eq(storei));  // open: gt, lt
  Comparator #(.width(12), .mode("unsigned")) comparator_5 (.a(IR[11:0]), .b({12{1'b0}}), .eq(_000));  // open: gt, lt
  Comparator #(.width(12), .mode("unsigned")) comparator_6 (.a(IR[11:0]), .b(12'h400), .eq(_400));  // open: gt, lt
  Comparator #(.width(12), .mode("unsigned")) comparator_7 (.a(IR[11:0]), .b(12'h800), .eq(_800));  // open: gt, lt
endmodule
