// Logisim project marie05.circ as structural Verilog: 5 circuits, main circuit main
module main (
  input  start,
  input  reset,
  output [15:0] out_3,
  output [11:0] out_4,
  output [15:0] out_5,
  output [11:0] out_6,
  output [15:0] out_7,
  output [15:0] out_8,
  output [15:0] out_9,
  output [15:0] out_10,
  output [15:0] out_11
);

  wire _000, _400, _800, AC_0, AC_0_t, AC__0, add, add1, add2, and_1_out, and_2_out, and_3_out, clear, clock,
       continue1, continue2, continue3, continue4, controlled_buffer_8_out, d_ff_2_q, d_ff_4_q, d_ff_9_q,
       d_ff_10_q, d_ff_11_q, d_ff_12_q, d_ff_13_q, d_ff_14_q, d_ff_16_q, d_ff_17_q, d_ff_18_q,
       demultiplexer_1_out0, demultiplexer_1_out1, demultiplexer_2_out0, demultiplexer_3_out0,
       demultiplexer_3_out1, demultiplexer_3_out2, demultiplexer_3_out3, demultiplexer_3_out4,
       demultiplexer_3_out7, demultiplexer_3_out8, demultiplexer_3_out10, demultiplexer_3_out11,
       demultiplexer_3_out12, demultiplexer_3_out13, demultiplexer_3_out14, demultiplexer_4_out0,
       demultiplexer_4_out1, demultiplexer_5_out0, demultiplexer_7_out1, demultiplexer_8_out1,
       demultiplexer_11_out0, demultiplexer_17_out0, done_operation, emp, enable_keyboard, enable_tty,
       end_jmp, fstate, idle_q, instruction_decoder_1_halt, is_add, is_addl, is_jnS, is_jumpl, is_load,
       is_loadi, is_store, is_storel, is_subt, l_AC, l_AC_0, l_AC_1, l_AC_2, l_AC_11, l_MAR, l_MAR0, l_MAR3,
       l_MAR9, l_MBR, l_MBR1, l_MBR4, l_MBR8, l_OUT, l_PC, l_PC1, l_PC2, l_PC6, ld0, mov_inst_to_IR_q,
       multiplexer_3_out, multiplexer_4_out, no_halt, or_1_out, or_2_out, or_5_out, or_6_out, or_7_out,
       or_8_out, or_10_out, or_15_out, or_17_out, or_19_out, or_23_out, or_25_out, or_29_out, or_32_out,
       or_33_out, or_34_out, or_36_out, or_37_out, or_38_out, or_39_out, or_40_out, or_41_out, phase, r_ins,
       read1, read2, read4, \repeat , s_AC, s_PC, skip, start_operation, start_q, start_reading1,
       start_writing0, store_data_mbr_q, store_data_mbr_to_ac_q, storel_work, sub, w_AC, w_continue1,
       w_continue2, w_iR, w_MBR, w_MBR5, w_PC, w_RAM, wait_obtain_data_q, wait_reading1, wait_write_data_q,
       wait_writing0, write_1;
  wire [2:0] counter_1_q;
  wire [11:0] branch_control_next_instruction, multiplexer_2_out;
  wire [15:0] AC_prime, keyborad_input, multiplexer_1_out;

  Register #(.width(16)) IN (.D(keyborad_input), .en(enable_keyboard), .Q(out_5), .clk(clock), .clr(reset));
  D_Flip_Flop idle (.clk(clock), .D(or_2_out), .Q(idle_q), .preset(reset));  // open: Qn, en, reset
  or or_1 (or_1_out, l_MAR9, l_PC1);
  or or_2 (or_2_out, demultiplexer_2_out0, demultiplexer_1_out0);
  Demultiplexer #(.enable("false")) demultiplexer_1 (
    .out0(demultiplexer_1_out0), .out1(demultiplexer_1_out1), .in(idle_q), .sel(start));
  or or_3 (start_operation, start_reading1, start_writing0);
  or or_4 (w_iR, l_MAR3, or_1_out);
  alu alu_1 (.AC(out_3), .MBR(out_9), .add(add), .sub(sub), .clear(clear), .AC_prime(AC_prime));
  assign out_11 = w_AC ? out_3 : 16'bz;  // Controlled_Buffer controlled_buffer_1
  assign out_11 = l_AC_1 ? out_5 : 16'bz;  // Controlled_Buffer controlled_buffer_2
  D_Flip_Flop u_start (.clk(clock), .D(demultiplexer_1_out1), .Q(start_q), .reset(reset));  // open: Qn, preset, en
  or or_5 (or_5_out, l_MBR8, l_MBR4);
  or or_6 (or_6_out, l_PC2, fstate, l_PC6, end_jmp, l_PC1);
  Multiplexer #(.width(16), .enable("false")) multiplexer_1 (
    .in0(out_11), .in1(AC_prime), .out(multiplexer_1_out), .sel(s_AC));
  or or_7 (or_7_out, start_q, \repeat );
  Demultiplexer #(.enable("false")) demultiplexer_2 (
    .out0(demultiplexer_2_out0), .out1(l_MAR0), .in(or_7_out), .sel(no_halt));
  or or_8 (or_8_out, emp, l_MAR9);
  or or_9 (l_MBR, continue1, l_MBR1, or_5_out);
  or or_10 (or_10_out, clear, add2);
  or or_11 (l_PC, continue4, or_6_out);
  Register #(.width(16)) OUT (.D(out_11), .en(l_OUT), .Q(out_7), .clk(clock), .clr(reset));
  or or_12 (l_MAR, l_MAR0, l_MAR3, or_8_out);
  or or_13 (w_PC, l_MAR0, l_MBR4);
  or or_14 (s_PC, continue4, or_15_out);
  or or_15 (or_15_out, l_PC2, l_PC6);
  or or_16 (s_AC, l_AC_2, or_10_out);
  Register #(.width(16)) AC (.D(multiplexer_1_out), .en(l_AC), .Q(out_3), .clk(clock), .clr(reset));
  TTY #(.rows(4), .cols(20)) tty_1 (.data(out_7[6:0]), .clk(clock), .we(enable_tty), .clr(reset));
  D_Flip_Flop read_instruction (.clk(clock), .D(l_MAR0), .Q(read4), .reset(reset));  // open: Qn, preset, en
  or or_17 (or_17_out, l_AC_11, emp, fstate);
  or or_18 (add, add1, add2);
  or or_19 (or_19_out, add2, clear, l_AC_11);
  instruction_decoder instruction_decoder_1 (
    .IR(out_8), .jumpi(is_jumpl), .loadi(is_loadi), .storei(is_storel), ._000(_000), ._400(_400),
    ._800(_800), .add(is_add), .JnS(is_jnS), .Load(is_load), .Store(is_store), .subt(is_subt),
    .halt(instruction_decoder_1_halt), .addi(is_addl));  // open: input, SkipCond, Jmp, output, Clear
  or or_20 (w_AC, l_MBR1, l_OUT, storel_work);
  or or_21 (l_AC, l_AC_0, l_AC_1, l_AC_2, or_19_out);
  or or_22 (w_MBR, l_AC_0, or_17_out, w_MBR5);
  assign out_11 = end_jmp ? {4'b0000, out_4} : 16'bz;  // Controlled_Buffer controlled_buffer_3
  assign out_11 = w_PC ? {4'b0000, out_6} : 16'bz;  // Controlled_Buffer controlled_buffer_4
  assign out_11 = w_iR ? out_8 : 16'bz;  // Controlled_Buffer controlled_buffer_5
  assign out_11 = w_MBR ? out_9 : 16'bz;  // Controlled_Buffer controlled_buffer_6
  assign out_11 = w_RAM ? out_10 : 16'bz;  // Controlled_Buffer controlled_buffer_7
  assign controlled_buffer_8_out = enable_keyboard ? clock : 1'bz;  // Controlled_Buffer controlled_buffer_8
  Comparator #(.width(16)) comparator_1 (.a(out_3), .b({16{1'b0}}), .gt(AC_0_t), .eq(AC__0), .lt(AC_0));
  Counter #(.width(3), .max('h7)) counter_1 (
    .Q(counter_1_q), .clk(controlled_buffer_8_out), .clr(reset));  // open: load, D, count, carry
  not not_1 (no_halt, instruction_decoder_1_halt);
  Register #(.width(12)) MAR (.D(out_11[11:0]), .en(l_MAR), .Q(out_4), .clk(clock), .clr(reset));
  branch_control branch_control (.actual_instruction(out_6), .next_instruction(branch_control_next_instruction));
  Register #(.width(16)) IR (.D(out_11), .en(continue4), .Q(out_8), .clk(clock), .clr(reset));
  Register #(.width(16)) MBR (.D(out_11), .en(l_MBR), .Q(out_9), .clk(clock), .clr(reset));
  or or_23 (or_23_out, continue4, 1'b0);
  or or_24 (w_RAM, continue4, continue1, or_25_out);
  buf or_25 (or_25_out, l_MBR8);  // OR_Gate
  Multiplexer #(.width(12), .enable("false")) multiplexer_2 (
    .in0(out_11[11:0]), .in1(branch_control_next_instruction), .out(multiplexer_2_out), .sel(s_PC));
  ram_asm ram_asm_1 (
    .address(out_4), .clock(clock), .start(start_operation), .ready(done_operation), .read_data(out_10),
    .data_to_write(out_11), .read_write(start_writing0));
  and and_1 (and_1_out, _400, AC__0);
  Register #(.width(12)) PC (.D(multiplexer_2_out), .en(l_PC), .Q(out_6), .clk(clock), .clr(reset));
  D_Flip_Flop mov_inst_to_IR (.clk(clock), .D(or_23_out), .Q(mov_inst_to_IR_q), .reset(reset));  // open: Qn, preset, en
  ROM #(.addrWidth(3), .dataWidth(16)) rom_1 (.addr(counter_1_q), .data(keyborad_input));  // open: sel
  and and_2 (and_2_out, _000, AC_0);
  and and_3 (and_3_out, AC_0_t, _800);
  or or_26 (skip, and_2_out, and_1_out, and_3_out);
  Clock clock_1 (.out(clock));
  Demultiplexer #(.select(4), .enable("false")) demultiplexer_3 (
    .out0(demultiplexer_3_out0), .out1(demultiplexer_3_out1), .out2(demultiplexer_3_out2),
    .out3(demultiplexer_3_out3), .out4(demultiplexer_3_out4), .out5(enable_keyboard), .out6(l_OUT),
    .out7(demultiplexer_3_out7), .out8(demultiplexer_3_out8), .out9(l_PC1), .out10(demultiplexer_3_out10),
    .out11(demultiplexer_3_out11), .out12(demultiplexer_3_out12), .out13(demultiplexer_3_out13),
    .out14(demultiplexer_3_out14), .in(mov_inst_to_IR_q), .sel(out_8[15:12]));  // open: out15
  or or_27 (l_MAR3, demultiplexer_3_out0, demultiplexer_3_out1, demultiplexer_3_out2, demultiplexer_3_out3, demultiplexer_3_out4);
  Demultiplexer #(.enable("false")) demultiplexer_4 (
    .out0(demultiplexer_4_out0), .out1(demultiplexer_4_out1), .in(demultiplexer_3_out8), .sel(skip));
  or or_28 (start_writing0, write_1, storel_work);
  Demultiplexer #(.enable("false")) demultiplexer_5 (
    .out0(demultiplexer_5_out0), .out1(read1), .in(l_MAR3), .sel(or_29_out));
  or or_29 (or_29_out, is_load, is_add, is_subt);
  D_Flip_Flop d_ff_1 (.clk(clock), .D(demultiplexer_4_out1), .Q(l_PC2), .reset(reset));  // open: Qn, preset, en
  or or_30 (start_reading1, read4, read1, read2, ld0);
  D_Flip_Flop d_ff_2 (.clk(clock), .D(demultiplexer_5_out0), .Q(d_ff_2_q), .reset(reset));  // open: Qn, preset, en
  Demultiplexer #(.enable("false")) demultiplexer_6 (.out0(l_MBR1), .out1(l_MBR4), .in(d_ff_2_q), .sel(is_jnS));
  D_Flip_Flop d_ff_3 (.clk(clock), .D(l_OUT), .Q(enable_tty), .reset(reset));  // open: Qn, preset, en
  D_Flip_Flop d_ff_4 (.clk(clock), .D(l_PC1), .Q(d_ff_4_q), .reset(reset));  // open: Qn, preset, en
  D_Flip_Flop d_ff_5 (.clk(clock), .D(demultiplexer_3_out10), .Q(clear), .reset(reset));  // open: Qn, preset, en
  or or_31 (l_MAR9, demultiplexer_3_out11, demultiplexer_3_out12, demultiplexer_3_out13, demultiplexer_3_out14);
  or or_32 (or_32_out, start_writing0, wait_writing0);
  or or_33 (or_33_out, start_reading1, wait_reading1);
  D_Flip_Flop d_ff_6 (.clk(clock), .D(enable_keyboard), .Q(l_AC_1), .reset(reset));  // open: Qn, preset, en
  D_Flip_Flop d_ff_7 (.clk(clock), .D(l_MAR9), .Q(read2), .reset(reset));  // open: Qn, preset, en
  D_Flip_Flop wait_write_data (
    .clk(clock), .D(or_32_out), .Q(wait_write_data_q), .reset(reset));  // open: Qn, preset, en
  D_Flip_Flop wait_obtain_data (
    .clk(clock), .D(or_33_out), .Q(wait_obtain_data_q), .reset(reset));  // open: Qn, preset, en
  Demultiplexer #(.enable("false")) demultiplexer_7 (
    .out0(wait_reading1), .out1(demultiplexer_7_out1), .in(wait_obtain_data_q), .sel(done_operation));
  D_Flip_Flop d_ff_8 (.clk(clock), .D(l_MBR4), .Q(w_MBR5), .reset(reset));  // open: Qn, preset, en
  D_Flip_Flop d_ff_9 (.clk(clock), .D(enable_tty), .Q(d_ff_9_q), .reset(reset));  // open: Qn, preset, en
  or or_34 (or_34_out, demultiplexer_4_out0, l_PC2);
  D_Flip_Flop d_ff_10 (.clk(clock), .D(clear), .Q(d_ff_10_q), .reset(reset));  // open: Qn, preset, en
  Demultiplexer #(.enable("false")) demultiplexer_8 (
    .out0(wait_writing0), .out1(demultiplexer_8_out1), .in(wait_write_data_q), .sel(done_operation));
  D_Flip_Flop d_ff_11 (.clk(clock), .D(l_AC_1), .Q(d_ff_11_q), .reset(reset));  // open: Qn, preset, en
  D_Flip_Flop d_ff_12 (.clk(clock), .D(or_34_out), .Q(d_ff_12_q), .reset(reset));  // open: Qn, preset, en
  Demultiplexer #(.enable("false")) demultiplexer_9 (.out0(l_AC_11), .out1(add2), .in(d_ff_13_q), .sel(is_addl));
  D_Flip_Flop d_ff_13 (.clk(clock), .D(continue3), .Q(d_ff_13_q), .reset(reset));  // open: Qn, preset, en
  Demultiplexer #(.enable("false")) demultiplexer_10 (
    .out0(w_continue1), .out1(w_continue2), .in(demultiplexer_8_out1), .sel(is_storel));
  Demultiplexer #(.enable("false")) demultiplexer_11 (
    .out0(demultiplexer_11_out0), .out1(continue4), .in(demultiplexer_7_out1), .sel(r_ins));
  or or_35 (write_1, l_MBR1, w_MBR5);
  Demultiplexer #(.enable("false")) demultiplexer_12 (
    .out0(l_MBR8), .out1(continue1), .in(demultiplexer_11_out0), .sel(or_36_out));
  or or_36 (or_36_out, is_add, is_load, is_subt);
  Demultiplexer #(.enable("false")) demultiplexer_13 (.out0(emp), .out1(fstate), .in(d_ff_14_q), .sel(is_jumpl));
  D_Flip_Flop d_ff_14 (.clk(clock), .D(continue2), .Q(d_ff_14_q), .reset(reset));  // open: Qn, preset, en
  Demultiplexer #(.enable("false")) demultiplexer_14 (.out0(continue2), .out1(continue3), .in(l_MBR8), .sel(phase));
  D_Flip_Flop store_data_mbr (.clk(clock), .D(continue1), .Q(store_data_mbr_q), .reset(reset));  // open: Qn, preset, en
  Demultiplexer #(.enable("false")) demultiplexer_15 (
    .out0(l_AC_2), .out1(l_AC_0), .in(store_data_mbr_q), .sel(is_load));
  Demultiplexer #(.enable("false")) demultiplexer_16 (.out0(sub), .out1(add1), .in(l_AC_2), .sel(is_add));
  Demultiplexer #(.enable("false")) demultiplexer_17 (
    .out0(demultiplexer_17_out0), .out1(end_jmp), .in(w_continue1), .sel(is_jnS));
  or or_37 (or_37_out, l_AC_11, add2, w_continue2, fstate);
  D_Flip_Flop d_ff_15 (.clk(clock), .D(end_jmp), .Q(l_PC6), .reset(reset));  // open: Qn, preset, en
  D_Flip_Flop d_ff_16 (.clk(clock), .D(emp), .Q(d_ff_16_q), .reset(reset));  // open: Qn, preset, en
  Demultiplexer #(.enable("false")) demultiplexer_18 (.out0(ld0), .out1(storel_work), .in(d_ff_16_q), .sel(is_storel));
  D_Flip_Flop d_ff_17 (.clk(clock), .D(or_37_out), .Q(d_ff_17_q), .reset(reset));  // open: Qn, preset, en
  or or_38 (or_38_out, sub, add1);
  D_Flip_Flop store_data_mbr_to_ac (
    .clk(clock), .D(l_AC_0), .Q(store_data_mbr_to_ac_q), .reset(reset));  // open: Qn, preset, en
  or or_39 (or_39_out, l_PC6, demultiplexer_17_out0, store_data_mbr_to_ac_q, or_38_out);
  D_Flip_Flop d_ff_18 (.clk(clock), .D(or_39_out), .Q(d_ff_18_q), .reset(reset));  // open: Qn, preset, en
  Multiplexer #(.enable("false")) multiplexer_3 (.in0(1'b0), .in1(1'b1), .out(multiplexer_3_out), .sel(l_MAR0));
  or or_40 (or_40_out, l_MAR0, continue4);
  Multiplexer #(.enable("false")) multiplexer_4 (.in0(1'b0), .in1(1'b1), .out(multiplexer_4_out), .sel(ld0));
  or or_41 (or_41_out, ld0, continue3);
  or or_42 (\repeat , d_ff_18_q, d_ff_11_q, d_ff_9_q, demultiplexer_3_out7, d_ff_12_q, d_ff_4_q, d_ff_10_q, d_ff_17_q);
  D_Flip_Flop d_ff_19 (
    .clk(clock), .D(multiplexer_3_out), .Q(r_ins), .en(or_40_out), .reset(reset));  // open: Qn, preset
  D_Flip_Flop d_ff_20 (
    .clk(clock), .D(multiplexer_4_out), .Q(phase), .en(or_41_out), .reset(reset));  // open: Qn, preset

  // Other names for the same wires on the sheet: AC[15:0] = out_3; ac_write_to_bus[15:0] = out_3; IN[15:0] = out_5;
  //   IR[15:0] = out_8; ir_write_to_bus[15:0] = out_8; l_IN = enable_keyboard; ld1 = continue3; MAR[11:0] = out_4;
  //   mar_write_to_bus[11:0] = out_4; MBR[15:0] = out_9; mbr_write_to_bus[15:0] = out_9; PC[11:0] = out_6;
  //   pc_write_to_bus[11:0] = out_6; ram_write_to_bus[15:0] = out_10; s_AC0 = l_AC_2; l_AC_4 = clear; s_AC2 = clear;
  //   l_AC_12 = add2; s_AC3 = add2; s_PC1 = l_PC2; s_PC4 = l_PC6; read3 = ld0; sl = ld0; w_AC0 = l_MBR1;
  //   w_AC1 = l_OUT; w_IN = l_AC_1; w_iR2 = l_MAR3; w_iR4 = l_PC1; w_iR9 = l_MAR9; l_PC5 = end_jmp; w_MAR = end_jmp;
  //   w_MAR0 = end_jmp; l_MAR10 = emp; w_MBR6 = emp; w_MBR11 = l_AC_11; l_PC12 = fstate; w_MBR12 = fstate;
  //   w_MBR_0 = l_AC_0; rld0 = l_MAR0; slr = l_MAR0; w_PC0 = l_MAR0; w_PC1 = l_MBR4; l_IR = continue4;
  //   l_IR0 = continue4; l_PC0 = continue4; rld1 = continue4; s_PC0 = continue4; w_RAM0 = continue4;
  //   l_MBR0 = continue1; w_RAM1 = continue1; w_RAM8 = l_MBR8; w_AC11 = storel_work; write_2 = storel_work;
  //   write_enable = start_writing0; write_enable0 = start_writing0

  // Notes on the sheet:
  //   Control Unit
  //   Data Bus
  //   Data Bus
  //   Data Bus
  //   Data Bus
  //   Data Bus
  //   Data Bus
  //   Data Bus
  //   contents of rom_1 (hex, n*v repeats v):
  //   7 2a 29 28 27 26 25 24
  //   Indirect Addressing
  //   Input
  //   Output
  //   Jump
  //   Storel
  //   Clear
  //   SkipCond
  //   Store
  //   Writing Instructions
  //   Reading Instructions
  //   JnS
  //   Loadl
  //   Addl
  //   Load
  //   Subt
  //   Add
  //   Jumpl
endmodule

module ram_asm (
  input  [11:0] address,
  input  clock,
  input  start,
  input  read_write,
  input  [15:0] data_to_write,
  output ready,
  output [15:0] read_data
);

  wire not_1_out;

  RAM #(.addrWidth(12), .dataWidth(16), .bus("separate")) ram_1 (
    .addr(address), .din(data_to_write), .data(read_data), .str(read_write), .clk(clock), .ld(not_1_out));  // open: sel, clr
  not not_1 (not_1_out, read_write);
  Counter #(.width(1), .max('h1)) counter_1 (.carry(ready), .clk(clock), .clr(start));  // open: load, D, count, Q
endmodule

module branch_control (
  input  [11:0] actual_instruction,
  output [11:0] next_instruction
);

  Adder #(.width(12)) adder_1 (.a(actual_instruction), .b(12'h1), .out(next_instruction));  // open: cin, cout
endmodule

module alu (
  input  [15:0] AC,
  input  [15:0] MBR,
  input  add,
  input  sub,
  input  clear,
  output [15:0] AC_prime
);

  wire [15:0] adder_1_out, subtractor_1_out;

  Adder #(.width(16)) adder_1 (.a(AC), .b(MBR), .out(adder_1_out));  // open: cin, cout
  Subtractor #(.width(16)) subtractor_1 (.a(AC), .b(MBR), .out(subtractor_1_out));  // open: bin, bout
  Multiplexer #(.select(3), .width(16), .enable("false")) multiplexer_1 (
    .in0({16{1'b0}}), .in1(adder_1_out), .in2(subtractor_1_out), .in3({16{1'b0}}), .in4({16{1'b0}}),
    .in5({16{1'b0}}), .in6({16{1'b0}}), .in7({16{1'b0}}), .out(AC_prime), .sel({clear, sub, add}));
endmodule

module instruction_decoder (
  input  [15:0] IR,
  output addi,
  output jumpi,
  output loadi,
  output storei,
  output JnS,
  output Load,
  output Store,
  output add,
  output subt,
  output \input ,
  output \output ,
  output halt,
  output SkipCond,
  output Jmp,
  output Clear,
  output _000,
  output _400,
  output _800
);

  Decoder #(.select(4), .enable("false")) decoder_1 (
    .out0(JnS), .out1(Load), .out2(Store), .out3(add), .out4(subt), .out5(\input ), .out6(\output ),
    .out7(halt), .out8(SkipCond), .out9(Jmp), .out10(Clear), .out11(addi), .out12(jumpi), .out13(loadi),
    .out14(storei), .sel(IR[15:12]));  // open: out15
  Comparator #(.width(12), .mode("unsigned")) comparator_1 (.a(IR[11:0]), .b({12{1'b0}}), .eq(_000));  // open: gt, lt
  Comparator #(.width(12), .mode("unsigned")) comparator_2 (.a(IR[11:0]), .b(12'h400), .eq(_400));  // open: gt, lt
  Comparator #(.width(12), .mode("unsigned")) comparator_3 (.a(IR[11:0]), .b(12'h800), .eq(_800));  // open: gt, lt
endmodule
