// Logisim project templates.circ as structural Verilog: 1 circuit, main circuit templates
module templates (
);

  wire clock, or_1_out, or_2_out, reset, undriven_2;
  wire [15:0] register_1_q, undriven;

  Demultiplexer #(.enable("false")) demultiplexer_1 (.in(or_1_out));  // open: out0, out1, sel
  buf or_1 (or_1_out, 1'b0);  // OR_Gate
  Register #(.width(16)) register_1 (.D(undriven), .en(undriven_2), .Q(register_1_q), .clk(clock), .clr(reset));
  buf or_2 (or_2_out, 1'b0);  // OR_Gate
  D_Flip_Flop d_ff_1 (.clk(clock), .D(or_2_out), .reset(reset));  // open: Q, Qn, preset, en
endmodule
