// Logisim project palindromo.circ as structural Verilog: 2 circuits, main circuit stack
module stack (
  input  \input ,
  input  pop,
  input  push,
  input  clock,
  input  reset,
  output top
);

  wire _0, _1, _2, _3, _4, _5, _6;
  wire [7:0] multiplexer_1_out;

  Multiplexer #(.select(2), .width(8), .enable("false")) multiplexer_1 (
    .in0({top, _6, _5, _4, _3, _2, _1, _0}), .in1({\input , top, _6, _5, _4, _3, _2, _1}),
    .in2({_6, _5, _4, _3, _2, _1, _0, 1'b0}), .out(multiplexer_1_out), .sel({pop, push}));  // open: in3
  Register memory (.D(multiplexer_1_out), .en(1'b1), .Q({top, _6, _5, _4, _3, _2, _1, _0}), .clk(clock), .clr(reset));

  // Other names for the same wires on the sheet: _7 = top; in0[7:0] = {top, _6, _5, _4, _3, _2, _1, _0};
  //   in1[7:0] = {\input , top, _6, _5, _4, _3, _2, _1}; in2[7:1] = {_6, _5, _4, _3, _2, _1, _0}
endmodule

module palindromo (
  input  [7:0] in_1,
  input  [2:0] in_2,
  input  in_3,
  input  in_4,
  input  in_5,
  output \output ,
  output \end 
);

  wire and_1_out, change_flag, comparator_2_eq, demultiplexer_1_out0, demultiplexer_3_out0,
       demultiplexer_3_out1, demultiplexer_4_out0, demultiplexer_5_out0, demultiplexer_5_out1, exit, i_len,
       idle_q, if_q, input_i, Li, Li0, Li1, Li2, Li3, multiplexer_2_out, or_2_out, or_4_out, or_5_out,
       or_7_out, or_8_out, pop, setupstack_q, sflag, Si, top, while_q;
  wire [2:0] i, i_1, multiplexer_1_out;

  Comparator #(.width(3), .mode("unsigned")) comparator_1 (.a(i), .b(in_2), .lt(i_len));  // open: gt, eq
  or or_1 (Si, Li1, Li3);
  or or_2 (or_2_out, demultiplexer_5_out1, demultiplexer_1_out0);
  D_Flip_Flop idle (.clk(in_4), .D(or_2_out), .Q(idle_q), .preset(in_3), .en(1'b1));  // open: Qn, reset
  Multiplexer #(.width(3), .enable("false")) multiplexer_1 (.in0(3'b000), .in1(i_1), .out(multiplexer_1_out), .sel(Si));
  Demultiplexer #(.enable("false")) demultiplexer_1 (.out0(demultiplexer_1_out0), .out1(Li0), .in(idle_q), .sel(in_5));
  Multiplexer #(.enable("false")) multiplexer_2 (.in0(1'b1), .in1(1'b0), .out(multiplexer_2_out), .sel(change_flag));
  or or_3 (sflag, change_flag, Li2);
  or or_4 (or_4_out, Li0, Li1);
  Register #(.width(3)) register_1 (.D(multiplexer_1_out), .en(Li), .Q(i), .clk(in_4));  // open: clr
  D_Flip_Flop setupstack (.clk(in_4), .D(or_4_out), .Q(setupstack_q), .en(1'b1), .reset(in_3));  // open: Qn, preset
  Demultiplexer #(.enable("false")) demultiplexer_2 (.out0(Li2), .out1(Li1), .in(setupstack_q), .sel(i_len));
  Adder #(.width(3)) adder_1 (.a(i), .b(3'b001), .out(i_1));  // open: cin, cout
  Register #(.width(1)) flag (.D(multiplexer_2_out), .en(sflag), .Q(\output ), .clk(in_4));  // open: clr
  Comparator #(.width(1), .mode("unsigned")) comparator_2 (.a(input_i), .b(top), .eq(comparator_2_eq));  // open: gt, lt
  BitSelector bitselector_1 (.in(in_1), .out(input_i), .sel(i));
  or or_5 (or_5_out, Li2, Li3);
  not not_1 (exit, comparator_2_eq);
  or or_6 (Li, Li0, Li1, Li2, Li3);
  D_Flip_Flop \while  (.clk(in_4), .D(or_5_out), .Q(while_q), .en(1'b1), .reset(in_3));  // open: Qn, preset
  Demultiplexer #(.enable("false")) demultiplexer_3 (
    .out0(demultiplexer_3_out0), .out1(demultiplexer_3_out1), .in(while_q), .sel(and_1_out));
  and and_1 (and_1_out, i_len, \output );
  or or_7 (or_7_out, demultiplexer_5_out0, demultiplexer_3_out0);
  D_Flip_Flop u_end (.clk(in_4), .D(or_7_out), .Q(\end ), .en(1'b1), .reset(in_3));  // open: Qn, preset
  Demultiplexer #(.enable("false")) demultiplexer_4 (
    .out0(demultiplexer_4_out0), .out1(change_flag), .in(if_q), .sel(exit));
  D_Flip_Flop \if  (.clk(in_4), .D(demultiplexer_3_out1), .Q(if_q), .en(1'b1), .reset(in_3));  // open: Qn, preset
  stack STACK (.\input (input_i), .pop(pop), .push(Li1), .clock(in_4), .reset(or_8_out), .top(top));
  or or_8 (or_8_out, in_3, in_5);
  Demultiplexer #(.enable("false")) demultiplexer_5 (
    .out0(demultiplexer_5_out0), .out1(demultiplexer_5_out1), .in(\end ), .sel(in_5));
  or or_9 (pop, change_flag, demultiplexer_4_out0);
  D_Flip_Flop after_if (.clk(in_4), .D(pop), .Q(Li3), .en(1'b1), .reset(in_3));  // open: Qn, preset

  // Other names for the same wires on the sheet: clock = in_4; flag = \output ; input[7:0] = in_1; len[2:0] = in_2;
  //   push = Li1; Si0 = Li1; reset = in_3; sflag0 = Li2; sflag1 = change_flag; Si1 = Li3; start = in_5
endmodule
