// Logisim project perfecto.circ as structural Verilog: 3 circuits, main circuit main
module main (
  input  [7:0] a,
  input  [7:0] b,
  input  start,
  input  reset,
  output [7:0] o,
  output out_6
);

  wire clock_out;

  Clock clock (.out(clock_out));
  resto resto_1 (.a(a), .b(b), .start(start), .reset(reset), .clock(clock_out), .\end (out_6), .\output (o));
endmodule

module resto (
  input  [7:0] a,
  input  start,
  input  [7:0] b,
  input  reset,
  input  clock,
  output [7:0] \output ,
  output \end 
);

  wire A__B, comparator_1_eq, comparator_1_gt, demultiplexer_1_out0, demultiplexer_2_out0,
       demultiplexer_3_out0, demultiplexer_3_out1, idle_q, LA, LA0, LA1, or_1_out, or_2_out, or_3_out,
       or_5_out, while_q;
  wire [7:0] A_B, B_t, multiplexer_1_out;

  or or_1 (or_1_out, start, reset);
  Multiplexer #(.width(8), .enable("false")) multiplexer_1 (.in0(a), .in1(A_B), .out(multiplexer_1_out), .sel(LA1));
  or or_2 (or_2_out, demultiplexer_3_out1, demultiplexer_1_out0);
  Demultiplexer #(.disabled(0), .enable("false")) demultiplexer_1 (
    .out0(demultiplexer_1_out0), .out1(LA0), .in(idle_q), .sel(start));
  D_Flip_Flop idle (.clk(clock), .D(or_2_out), .Q(idle_q), .preset(or_1_out), .en(1'b1));  // open: Qn, reset
  Register register_1 (.D(multiplexer_1_out), .en(LA), .Q(\output ), .clk(clock));  // open: clr
  Subtractor subtractor_1 (.a(\output ), .b(B_t), .out(A_B));  // open: bin, bout
  Register register_2 (.D(b), .en(LA0), .Q(B_t), .clk(clock));  // open: clr
  Comparator comparator_1 (.a(\output ), .b(B_t), .gt(comparator_1_gt), .eq(comparator_1_eq));  // open: lt
  or or_3 (or_3_out, LA0, LA1);
  or or_4 (A__B, comparator_1_gt, comparator_1_eq);
  D_Flip_Flop \while  (.clk(clock), .D(or_3_out), .Q(while_q), .en(1'b1), .reset(reset));  // open: Qn, preset
  Demultiplexer #(.enable("false")) demultiplexer_2 (.out0(demultiplexer_2_out0), .out1(LA1), .in(while_q), .sel(A__B));
  D_Flip_Flop u_end (.clk(clock), .D(or_5_out), .Q(\end ), .en(1'b1), .reset(reset));  // open: Qn, preset
  or or_5 (or_5_out, demultiplexer_3_out0, demultiplexer_2_out0);
  or or_6 (LA, LA0, LA1);
  Demultiplexer #(.enable("false")) demultiplexer_3 (
    .out0(demultiplexer_3_out0), .out1(demultiplexer_3_out1), .in(\end ), .sel(start));

  // Other names for the same wires on the sheet: A_t[7:0] = \output ; LB = LA0; SA = LA1
endmodule

module perfecto (
  input  [7:0] n,
  input  start,
  input  reset,
  input  clock,
  output \output ,
  output \end 
);

  wire c_n, demultiplexer_1_out0, demultiplexer_2_out0, demultiplexer_3_out0, demultiplexer_3_out1,
       demultiplexer_4_out0, demultiplexer_4_out1, demultiplexer_5_out0, idle_q, LC, LC0, LC1, Ls, Ls1,
       or_1_out, or_3_out, or_4_out, or_5_out, or_7_out, or_8_out, ready, rem_0, start_rem, wait_q, while_q;
  wire [7:0] adder_1_out, adder_2_out, c, multiplexer_1_out, multiplexer_2_out, N_t, remainder, s;

  or or_1 (or_1_out, demultiplexer_3_out1, demultiplexer_1_out0);
  or or_2 (Ls, LC0, Ls1);
  D_Flip_Flop idle (.clk(clock), .D(or_1_out), .Q(idle_q), .preset(or_3_out), .en(1'b1));  // open: Qn, reset
  or or_3 (or_3_out, start, reset);
  Register register_1 (.D(n), .en(LC0), .Q(N_t), .clk(clock));  // open: clr
  Adder adder_1 (.a(8'h1), .b(c), .out(adder_1_out));  // open: cin, cout
  resto resto (.a(N_t), .b(c), .start(start_rem), .clock(clock), .\end (ready), .\output (remainder));  // open: reset
  Demultiplexer #(.enable("false")) demultiplexer_1 (.out0(demultiplexer_1_out0), .out1(LC0), .in(idle_q), .sel(start));
  Adder adder_2 (.a(s), .b(c), .out(adder_2_out));  // open: cin, cout
  Comparator comparator_1 (.a(c), .b(N_t), .lt(c_n));  // open: gt, eq
  Multiplexer #(.width(8), .enable("false")) multiplexer_1 (
    .in0(8'h1), .in1(adder_1_out), .out(multiplexer_1_out), .sel(LC1));
  Register register_2 (.D(multiplexer_1_out), .en(LC), .Q(c), .clk(clock));  // open: clr
  or or_4 (or_4_out, LC0, LC1);
  Multiplexer #(.width(8), .enable("false")) multiplexer_2 (
    .in0({8{1'b0}}), .in1(adder_2_out), .out(multiplexer_2_out), .sel(Ls1));
  Demultiplexer #(.enable("false")) demultiplexer_2 (
    .out0(demultiplexer_2_out0), .out1(start_rem), .in(while_q), .sel(c_n));
  D_Flip_Flop \while  (.clk(clock), .D(or_4_out), .Q(while_q), .en(1'b1), .reset(reset));  // open: Qn, preset
  Register register_3 (.D(multiplexer_2_out), .en(Ls), .Q(s), .clk(clock));  // open: clr
  or or_5 (or_5_out, demultiplexer_3_out0, demultiplexer_2_out0);
  or or_6 (LC, LC0, LC1);
  Comparator comparator_2 (.a(s), .b(N_t), .eq(\output ));  // open: gt, lt
  Comparator comparator_3 (.a(remainder), .b({8{1'b0}}), .eq(rem_0));  // open: gt, lt
  Demultiplexer #(.enable("false")) demultiplexer_3 (
    .out0(demultiplexer_3_out0), .out1(demultiplexer_3_out1), .in(\end ), .sel(start));
  D_Flip_Flop u_end (.clk(clock), .D(or_5_out), .Q(\end ), .en(1'b1), .reset(reset));  // open: Qn, preset
  or or_7 (or_7_out, start_rem, demultiplexer_4_out0);
  Demultiplexer #(.enable("false")) demultiplexer_4 (
    .out0(demultiplexer_4_out0), .out1(demultiplexer_4_out1), .in(wait_q), .sel(ready));
  D_Flip_Flop \wait  (.clk(clock), .D(or_7_out), .Q(wait_q), .en(1'b1), .reset(reset));  // open: Qn, preset
  Demultiplexer #(.enable("false")) demultiplexer_5 (
    .out0(demultiplexer_5_out0), .out1(Ls1), .in(demultiplexer_4_out1), .sel(rem_0));
  or or_8 (or_8_out, demultiplexer_5_out0, Ls1);
  D_Flip_Flop after_if (.clk(clock), .D(or_8_out), .Q(LC1), .en(1'b1), .reset(reset));  // open: Qn, preset

  // Other names for the same wires on the sheet: LN = LC0; Ls0 = LC0; Sc = LC1; Ss = Ls1
endmodule
